// Logisim project RC_1_redsgn.circ as structural Verilog
module main (
  output [23:0] Sequnce,
  output [15:0] Adress_Bus
);

  wire button_1_out, clock_1_out, COND_CARRY, COND_CARRY_REG, COND_SIGN, COND_SIGN_REG, COND_ZERO,
       COND_ZERO_REG, digital_oscilloscope_1_p3, fetch_1_incsel, fetch_1_linc, fetch_1_linstr, fetch_1_mer,
       fetch_1_pcload, fetch_1_pcsel, instr_decoder_1_goto, instr_decoder_1_mov8, instructions_1_aload,
       instructions_1_bload, instructions_1_j1_load, instructions_1_j2_load, instructions_1_j_sel,
       instructions_1_m1_load, instructions_1_m2_load, instructions_1_m_sel, n7404_1_pin2, n7404_2_pin6,
       n7404_2_pin8, n7404_2_pin9, n7408_1_pin2, n7408_1_pin3, n7408_1_pin4, n7408_1_pin6, n7408_1_pin8,
       n7408_1_pin9, n7408_2_pin8, n7432_1_pin1, n7432_1_pin2, n7432_1_pin3, n7432_1_pin4, n7432_1_pin5,
       n7432_1_pin6, n7432_1_pin8, n7432_1_pin10, n7432_2_pin2, n7432_2_pin3, n7432_2_pin5, n7432_2_pin6,
       n7432_2_pin8, n7432_2_pin9, n7432_2_pin11, n7432_2_pin13, n7432_3_pin2, n7432_3_pin3, n7432_4_pin3,
       n7432_4_pin4, n7432_4_pin6, n7432_4_pin11, n7432_5_pin3, n7432_5_pin6, n7474_1_pin1, n74164_1_pin8,
       n74165_1_pin9, n74165_2_pin9, n74165_2_pin11, n74165_2_pin12, n74193_1_pin4, n74193_1_pin7,
       n74193_1_pin14, n74193_2_pin6, n74245_1_pin1, ram_1_p3, SEQ_AT08;
  wire [3:0] output_register_1_disp_out, output_register_1_disp_out_2;
  wire [7:0] Data_Bus, dual_regist_b_c_3_bout, dual_regist_b_c_3_cout, gate_8_1_dout, Instr_Bus,
       instructions_1_dout, instructions_1_reg_load, instructions_1_reg_select, output_register_1_reg_select;

  Button button_1 (.out(button_1_out));
  Clock clock_1 (.out(clock_1_out));
  _7432 #(.ShowInternalStructure("true")) u_7432_1 (
    .pin1(n7432_1_pin1), .pin2(n7432_1_pin2), .pin3(n7432_1_pin3), .pin4(n7432_1_pin4), .pin5(n7432_1_pin5),
    .pin6(n7432_1_pin6), .pin10(n7432_1_pin10), .pin9(n7432_1_pin6), .pin8(n7432_1_pin8));  // open: pin13, pin12, pin11
  SEQUENCER sequencer_1 (
    .START(button_1_out), .CLOCK(clock_1_out), .AT08(instr_decoder_1_mov8), .AT10(n7432_1_pin8),
    .AT12(n7432_1_pin3), .SQC(Sequnce));  // open: AT14
  GATE_8 gate_8_1 (.EN(n7432_1_pin4), .DIn(Instr_Bus), .DOut(gate_8_1_dout));
  _7408 #(.ShowInternalStructure("true")) u_7408_1 (
    .pin1(n7432_1_pin4), .pin2(n7408_1_pin2), .pin3(n7408_1_pin3), .pin4(n7408_1_pin4), .pin5(n7432_1_pin4),
    .pin6(n7408_1_pin6), .pin13(clock_1_out), .pin10(n7432_1_pin5), .pin9(n7408_1_pin9), .pin8(n7408_1_pin8));  // open: pin12, pin11
  ALU alu_1 (
    .BIn(dual_regist_b_c_3_bout), .CIn(dual_regist_b_c_3_cout), .INSTR(gate_8_1_dout), .SQC(Sequnce),
    .A(n7408_1_pin4), .D(n7408_1_pin2), .DOut(Data_Bus), .Sign(COND_SIGN), .Zero(COND_ZERO), .Cry(COND_CARRY));
  Fetch fetch_1 (
    .SQC(Sequnce), .PCSEL(fetch_1_pcsel), .MER(fetch_1_mer), .LINC(fetch_1_linc), .LINSTR(fetch_1_linstr),
    .INCSEL(fetch_1_incsel), .PCLOAD(fetch_1_pcload));
  _7432 #(.ShowInternalStructure("true")) u_7432_2 (
    .pin1(fetch_1_pcsel), .pin2(n7432_2_pin2), .pin3(n7432_2_pin3), .pin4(fetch_1_pcload),
    .pin5(n7432_2_pin5), .pin6(n7432_2_pin6), .pin13(n7432_2_pin13), .pin12(fetch_1_linc),
    .pin11(n7432_2_pin11), .pin10(fetch_1_incsel), .pin9(n7432_2_pin9), .pin8(n7432_2_pin8));
  _7432 #(.ShowInternalStructure("true")) u_7432_3 (
    .pin1(fetch_1_mer), .pin2(n7432_3_pin2), .pin3(n7432_3_pin3));  // open: pin4, pin5, pin6, pin13, pin12, pin11, pin10, pin9, pin8
  // RAM #(.addrWidth(16), .databus("bidir"), .enables("line")) ram_1: pin names not known; wires that end beside it: Adress_Bus, n7432_3_pin3, ram_1_p3, clock_1_out, Data_Bus
  Incrementer incrementer_1 (
    .CLK(clock_1_out), .LoadINC(n7432_2_pin11), .AIn(Adress_Bus), .SELECTINC(n7432_2_pin8), .AOut(Adress_Bus));
  _7408 #(.ShowInternalStructure("true")) u_7408_2 (
    .pin10(clock_1_out), .pin9(n7432_1_pin4), .pin8(n7408_2_pin8));  // open: pin1, pin2, pin3, pin4, pin5, pin6, pin13, pin12, pin11
  INSTRUCTIONS instructions_1 (
    .MOV_8(instr_decoder_1_mov8), .SQC(Sequnce), .INSTR(Instr_Bus), .LOAD_8(n7432_1_pin2),
    .F({COND_SIGN_REG, COND_ZERO_REG, COND_CARRY_REG}), .SAVE_8(n7432_1_pin1), .SET_AB(n7432_1_pin5),
    .GOTO_16(instr_decoder_1_goto), .REG_IN(output_register_1_reg_select),
    .REG_SELECT(instructions_1_reg_select), .REG_LOAD(instructions_1_reg_load), .M_SEL(instructions_1_m_sel),
    .PC_SEL(n7432_2_pin2), .MEW(ram_1_p3), .MER(n7432_3_pin2), .ALOAD(instructions_1_aload),
    .BLOAD(instructions_1_bload), .DOut(instructions_1_dout), .J1_LOAD(instructions_1_j1_load),
    .M1_LOAD(instructions_1_m1_load), .J2_LOAD(instructions_1_j2_load), .M2_LOAD(instructions_1_m2_load),
    .INC_LOAD(n7432_2_pin13), .J_SEL(instructions_1_j_sel), .PC_LOAD(n7432_2_pin5), .INC_SEL(n7432_2_pin9),
    .AT_08(SEQ_AT08));
  _7432 #(.ShowInternalStructure("true")) u_7432_4 (
    .pin1(instructions_1_bload), .pin2(instructions_1_reg_load[6]), .pin3(n7432_4_pin3), .pin4(n7432_4_pin4),
    .pin5(instructions_1_aload), .pin6(n7432_4_pin6), .pin13(n7408_1_pin3),
    .pin12(instructions_1_reg_load[4]), .pin11(n7432_4_pin11), .pin10(n7408_1_pin6),
    .pin9(instructions_1_reg_load[7]), .pin8(n7432_4_pin4));
  _7474 #(.ShowInternalStructure("true")) u_7474_1 (
    .pin1(n7474_1_pin1), .pin2(COND_CARRY), .pin3(n7408_2_pin8), .pin5(COND_CARRY_REG), .pin13(n7474_1_pin1),
    .pin12(COND_ZERO), .pin11(n7408_2_pin8), .pin9(COND_ZERO_REG));  // open: pin4, pin6, pin10, pin8
  _7404 #(.ShowInternalStructure("true")) u_7404_1 (
    .pin1(n7408_1_pin8), .pin2(n7404_1_pin2), .pin3(n7432_3_pin3), .pin4(n7408_1_pin9));  // open: pin5, pin6, pin13, pin12, pin11, pin10, pin9, pin8
  Pull_Resistor pull_resistor_1 (.node(instructions_1_reg_load));
  Dual_Regist_B_C dual_regist_b_c_1 (
    .CLK(clock_1_out), .LOAD12(n7432_2_pin6), .SELECT12(n7432_2_pin3), .D16In(Adress_Bus), .D16Out(Adress_Bus));  // open: DIn, LOAD1, LOAD2, SELECT1, SELECT2, BOut, COut
  _7474 #(.ShowInternalStructure("true")) u_7474_2 (
    .pin1(n7474_1_pin1), .pin2(COND_SIGN), .pin3(n7408_2_pin8), .pin5(COND_SIGN_REG), .pin13(n7474_1_pin1),
    .pin12(n7474_1_pin1), .pin11(n7408_2_pin8));  // open: pin4, pin6, pin10, pin9, pin8
  Pull_Resistor pull_resistor_2 (.node(instructions_1_reg_select));
  Dual_Regist_B_C dual_regist_b_c_2 (
    .DIn(Data_Bus), .CLK(clock_1_out), .LOAD1(fetch_1_linstr), .BOut(Instr_Bus));  // open: LOAD2, SELECT1, SELECT2, LOAD12, SELECT12, D16In, COut, D16Out
  _74245 #(.ShowInternalStructure("true")) u_74245_1 (
    .pin1(n74245_1_pin1), .pin2(instructions_1_dout[0]), .pin3(instructions_1_dout[1]),
    .pin4(instructions_1_dout[2]), .pin5(instructions_1_dout[3]), .pin6(instructions_1_dout[4]),
    .pin7(instructions_1_dout[5]), .pin8(instructions_1_dout[6]), .pin9(instructions_1_dout[7]),
    .pin19(n7404_1_pin2), .pin18(Data_Bus[0]), .pin17(Data_Bus[1]), .pin16(Data_Bus[2]), .pin15(Data_Bus[3]),
    .pin14(Data_Bus[4]), .pin13(Data_Bus[5]), .pin12(Data_Bus[6]), .pin11(Data_Bus[7]));
  Instr_Decoder instr_decoder_1 (
    .in_1(Instr_Bus), .setab(n7432_1_pin5), .mov8(instr_decoder_1_mov8), .goto(instr_decoder_1_goto),
    .alu(n7432_1_pin4), .load(n7432_1_pin2), .store(n7432_1_pin1), .OUT_8(n7432_1_pin10));  // open: mov16, HALT, inc
  Dual_Register dual_register_1 (
    .DIn(Data_Bus), .CLK(clock_1_out), .LOAD1(n7432_4_pin6), .LOAD2(n7432_4_pin11),
    .SELECT1(instructions_1_reg_select[0]), .SELECT2(instructions_1_reg_select[3]), .DOut(Data_Bus));  // open: LOAD12, SELECT12, D16In, D16Out
  Dual_Regist_B_C dual_regist_b_c_3 (
    .DIn(Data_Bus), .CLK(clock_1_out), .LOAD1(n7432_4_pin3), .LOAD2(instructions_1_reg_load[5]),
    .SELECT1(instructions_1_reg_select[1]), .SELECT2(instructions_1_reg_select[2]),
    .BOut(dual_regist_b_c_3_bout), .COut(dual_regist_b_c_3_cout));  // open: LOAD12, SELECT12, D16In, D16Out
  _7432 #(.ShowInternalStructure("true")) u_7432_5 (
    .pin1(instructions_1_m1_load), .pin2(instructions_1_reg_load[1]), .pin3(n7432_5_pin3),
    .pin4(instructions_1_m2_load), .pin5(instructions_1_reg_load[0]), .pin6(n7432_5_pin6));  // open: pin13, pin12, pin11, pin10, pin9, pin8
  Dual_Register XY_Register (
    .DIn(Data_Bus), .CLK(clock_1_out), .LOAD1(instructions_1_reg_load[3]),
    .LOAD2(instructions_1_reg_load[2]), .SELECT1(instructions_1_reg_select[4]),
    .SELECT2(instructions_1_reg_select[5]), .D16In(Adress_Bus), .DOut(Data_Bus), .D16Out(Adress_Bus));  // open: LOAD12, SELECT12
  Dual_Register M_Register (
    .DIn(Data_Bus), .CLK(clock_1_out), .LOAD1(n7432_5_pin3), .LOAD2(n7432_5_pin6),
    .SELECT1(instructions_1_reg_select[6]), .SELECT2(instructions_1_reg_select[7]),
    .SELECT12(instructions_1_m_sel), .D16In(Adress_Bus), .DOut(Data_Bus), .D16Out(Adress_Bus));  // open: LOAD12
  Dual_Register J_Register (
    .DIn(Data_Bus), .CLK(clock_1_out), .LOAD1(instructions_1_j1_load), .LOAD2(instructions_1_j2_load),
    .SELECT12(instructions_1_j_sel), .D16Out(Adress_Bus));  // open: SELECT1, SELECT2, LOAD12, D16In, DOut
  _7404 #(.ShowInternalStructure("true")) u_7404_2 (
    .pin5(clock_1_out), .pin6(n7404_2_pin6), .pin9(n7404_2_pin9), .pin8(n7404_2_pin8));  // open: pin1, pin2, pin3, pin4, pin13, pin12, pin11, pin10
  Output_Register output_register_1 (
    .DIn(Data_Bus), .CLK(clock_1_out), .OUT8(n7432_1_pin10), .INSTR(Instr_Bus), .SQC(Sequnce),
    .DISP_OUT({output_register_1_disp_out_2, output_register_1_disp_out}),
    .REG_SELECT(output_register_1_reg_select));
  _74193 #(.ShowInternalStructure("true")) u_74193_1 (
    .pin4(n74193_1_pin4), .pin5(clock_1_out), .pin7(n74193_1_pin7), .pin15(n74193_1_pin4),
    .pin14(n74193_1_pin14), .pin11(n74193_1_pin4));  // open: pin1, pin2, pin3, pin6, pin13, pin12, pin10, pin9
  _74193 #(.ShowInternalStructure("true")) u_74193_2 (
    .pin2(n74193_1_pin14), .pin3(n7404_2_pin9), .pin4(n74193_1_pin4), .pin5(n74193_1_pin7),
    .pin6(n74193_2_pin6), .pin14(n74193_1_pin14), .pin11(n74193_1_pin4));  // open: pin1, pin7, pin15, pin13, pin12, pin10, pin9
  Keyboard keyboard_1 (.clk(clock_1_out));  // open: re, clr, avail, data
  Hex_Digit_Display hex_digit_display_1 (.value(output_register_1_disp_out_2));  // open: dp
  Hex_Digit_Display hex_digit_display_2 (.value(output_register_1_disp_out));  // open: dp
  _74165 #(.ShowInternalStructure("true")) u_74165_1 (
    .pin1(n7404_2_pin9), .pin2(n7404_2_pin6), .pin3(output_register_1_disp_out_2[0]),
    .pin4(output_register_1_disp_out_2[1]), .pin5(output_register_1_disp_out_2[2]),
    .pin6(output_register_1_disp_out_2[3]), .pin15(n7404_2_pin8), .pin14(output_register_1_disp_out[3]),
    .pin13(output_register_1_disp_out[2]), .pin12(output_register_1_disp_out[1]),
    .pin11(output_register_1_disp_out[0]), .pin9(n74165_1_pin9));  // open: pin7, pin10
  _74165 #(.ShowInternalStructure("true")) u_74165_2 (
    .pin1(n7404_2_pin9), .pin2(n7404_2_pin6), .pin15(n7404_2_pin8), .pin12(n74165_2_pin12),
    .pin11(n74165_2_pin11), .pin10(n74165_1_pin9), .pin9(n74165_2_pin9));  // open: pin3, pin4, pin5, pin6, pin7, pin14, pin13
  // LedBar #(.inputtype("row")) ledbar_1: pin names not known; wires that end beside it: n7432_1_pin10, n74165_2_pin11, {output_register_1_disp_out_2, output_register_1_disp_out}
  _74164 #(.ShowInternalStructure("true")) u_74164_1 (
    .pin1(n74165_2_pin9), .pin2(n74165_2_pin9), .pin9(n74165_2_pin12), .pin8(n74164_1_pin8));  // open: pin3, pin4, pin5, pin6, pin13, pin12, pin11, pin10
  TTY tty_1 (
    .data({output_register_1_disp_out_2[2:0], output_register_1_disp_out}), .clk(n7432_1_pin10));  // open: we, clr
  _7408 #(.ShowInternalStructure("true")) u_7408_3 (
    .pin10(clock_1_out), .pin9(n7404_2_pin9), .pin8(n74164_1_pin8));  // open: pin1, pin2, pin3, pin4, pin5, pin6, pin13, pin12, pin11
  // Digital_Oscilloscope #(.nState(14)) digital_oscilloscope_1: pin names not known; wires that end beside it: clock_1_out, n74165_2_pin9, digital_oscilloscope_1_p3
  _7486 #(.ShowInternalStructure("true")) u_7486_1 (
    .pin4(n74165_2_pin9), .pin5(clock_1_out), .pin6(digital_oscilloscope_1_p3));  // open: pin1, pin2, pin3, pin13, pin12, pin11, pin10, pin9, pin8
  // also tied to GND on the sheet: n74165_2_pin11
  // also tied to VCC on the sheet: {n7474_1_pin1, n74245_1_pin1, n74193_1_pin4, n74165_2_pin12}
endmodule

module SEQUENCER (
  input  START,
  input  CLOCK,
  input  AT08,
  input  AT10,
  input  AT12,
  input  AT14,
  output [23:0] SQC
);

  wire n7404_1_pin1, n7404_1_pin2, n7404_1_pin3, n7404_1_pin4, n7404_1_pin6, n7404_1_pin8, n7404_1_pin9,
       n7404_1_pin10, n7404_1_pin11, n7432_1_pin3, n7432_1_pin6, n7432_1_pin8, n7432_1_pin11, n7432_2_pin3,
       n7432_2_pin6, n7432_2_pin8, n7432_2_pin11, n7432_2_pin12, n7432_2_pin13, n7432_3_pin1, n7432_3_pin2,
       n7432_3_pin4, n7432_3_pin5, n7432_3_pin9, n7432_3_pin11, n7432_4_pin1, n7432_4_pin2, n7432_4_pin3,
       n7432_4_pin5, n7432_4_pin6, n7432_4_pin10, n7432_5_pin3, n7432_5_pin11, n7432_6_pin3;

  _7432 #(.ShowInternalStructure("true")) u_7432_1 (
    .pin1(SQC[7]), .pin2(SQC[6]), .pin3(n7432_1_pin3), .pin4(SQC[5]), .pin5(SQC[4]), .pin6(n7432_1_pin6),
    .pin13(SQC[3]), .pin12(SQC[2]), .pin11(n7432_1_pin11), .pin10(SQC[1]), .pin9(SQC[0]), .pin8(n7432_1_pin8));
  _7432 #(.ShowInternalStructure("true")) u_7432_2 (
    .pin1(n7432_1_pin3), .pin2(n7432_1_pin6), .pin3(n7432_2_pin3), .pin4(n7432_2_pin3), .pin5(n7432_1_pin11),
    .pin6(n7432_2_pin6), .pin13(n7432_2_pin13), .pin12(n7432_2_pin12), .pin11(n7432_2_pin11),
    .pin10(n7432_1_pin8), .pin9(n7432_2_pin6), .pin8(n7432_2_pin8));
  _7432 #(.ShowInternalStructure("true")) u_7432_3 (
    .pin1(n7432_3_pin1), .pin2(n7432_3_pin2), .pin3(n7432_2_pin13), .pin4(n7432_3_pin4), .pin5(n7432_3_pin5),
    .pin6(n7432_3_pin2), .pin13(START), .pin12(SQC[23]), .pin11(n7432_3_pin11), .pin10(n7432_3_pin11),
    .pin9(n7432_3_pin9), .pin8(n7432_3_pin4));
  _7404 #(.ShowInternalStructure("true")) u_7404_1 (
    .pin1(n7404_1_pin1), .pin2(n7404_1_pin2), .pin3(n7404_1_pin3), .pin4(n7404_1_pin4), .pin5(n7432_2_pin8),
    .pin6(n7404_1_pin6), .pin11(n7404_1_pin11), .pin10(n7404_1_pin10), .pin9(n7404_1_pin9),
    .pin8(n7404_1_pin8));  // open: pin13, pin12
  _7432 #(.ShowInternalStructure("true")) u_7432_4 (
    .pin1(n7432_4_pin1), .pin2(n7432_4_pin2), .pin3(n7432_4_pin3), .pin4(n7432_4_pin3), .pin5(n7432_4_pin5),
    .pin6(n7432_4_pin6), .pin10(n7432_4_pin10), .pin9(n7432_4_pin6), .pin8(n7404_1_pin9));  // open: pin13, pin12, pin11
  _74273 #(.ShowInternalStructure("true")) u_74273_1 (
    .pin1(n7404_1_pin8), .pin2(SQC[0]), .pin3(n7432_2_pin11), .pin4(SQC[0]), .pin5(SQC[1]), .pin6(SQC[2]),
    .pin7(SQC[1]), .pin8(SQC[2]), .pin9(SQC[3]), .pin19(SQC[7]), .pin18(SQC[6]), .pin17(SQC[5]),
    .pin16(SQC[6]), .pin15(SQC[5]), .pin14(SQC[4]), .pin13(SQC[3]), .pin12(SQC[4]), .pin11(CLOCK));
  _7408 #(.ShowInternalStructure("true")) u_7408_1 (
    .pin1(SQC[14]), .pin2(AT14), .pin3(n7432_4_pin10), .pin4(AT12), .pin5(SQC[12]), .pin6(n7432_4_pin5),
    .pin13(AT08), .pin12(SQC[8]), .pin11(n7432_4_pin2), .pin10(SQC[10]), .pin9(AT10), .pin8(n7432_4_pin1));
  _7408 #(.ShowInternalStructure("true")) u_7408_2 (
    .pin1(AT14), .pin2(n7404_1_pin10), .pin3(n7432_2_pin12), .pin4(AT12), .pin5(n7404_1_pin2),
    .pin6(n7432_3_pin1), .pin13(AT08), .pin12(n7404_1_pin6), .pin11(n7432_3_pin9), .pin10(AT10),
    .pin9(n7404_1_pin4), .pin8(n7432_3_pin5));
  _74273 #(.ShowInternalStructure("true")) u_74273_2 (
    .pin1(n7404_1_pin8), .pin2(SQC[8]), .pin3(SQC[7]), .pin4(SQC[8]), .pin5(SQC[9]), .pin6(SQC[10]),
    .pin7(SQC[9]), .pin8(SQC[10]), .pin9(SQC[11]), .pin19(SQC[15]), .pin18(SQC[14]), .pin17(SQC[13]),
    .pin16(SQC[14]), .pin15(SQC[13]), .pin14(SQC[12]), .pin13(SQC[11]), .pin12(SQC[12]), .pin11(CLOCK));
  _7432 #(.ShowInternalStructure("true")) u_7432_5 (
    .pin1(n7404_1_pin3), .pin2(SQC[10]), .pin3(n7432_5_pin3), .pin4(n7432_5_pin3), .pin5(SQC[11]),
    .pin6(n7404_1_pin1), .pin13(SQC[8]), .pin12(SQC[9]), .pin11(n7432_5_pin11), .pin10(n7432_5_pin11),
    .pin9(n7432_2_pin8), .pin8(n7404_1_pin3));
  _74273 #(.ShowInternalStructure("true")) u_74273_3 (
    .pin1(n7404_1_pin8), .pin2(SQC[16]), .pin3(SQC[15]), .pin4(SQC[16]), .pin5(SQC[17]), .pin6(SQC[18]),
    .pin7(SQC[17]), .pin8(SQC[18]), .pin9(SQC[19]), .pin19(SQC[23]), .pin18(SQC[22]), .pin17(SQC[21]),
    .pin16(SQC[22]), .pin15(SQC[21]), .pin14(SQC[20]), .pin13(SQC[19]), .pin12(SQC[20]), .pin11(CLOCK));
  _7432 #(.ShowInternalStructure("true")) u_7432_6 (
    .pin1(n7404_1_pin1), .pin2(SQC[12]), .pin3(n7432_6_pin3), .pin4(n7432_6_pin3), .pin5(SQC[13]),
    .pin6(n7404_1_pin11));  // open: pin13, pin12, pin11, pin10, pin9, pin8
endmodule

// ALU
module ALU1 (
  input  [7:0] BIn,
  input  CarryIn,
  input  [7:0] CIn,
  output CarryOut,
  output [7:0] SumOut
);

  wire n7408_1_pin3, n7408_1_pin6, n7408_1_pin8, n7408_1_pin11, n7408_3_pin3, n7408_3_pin6, n7408_3_pin8,
       n7408_3_pin11, n7432_1_pin4, n7432_1_pin5, n7432_1_pin6, n7432_1_pin8, n7432_1_pin9, n7432_1_pin10,
       n7432_1_pin11, n7432_2_pin4, n7432_2_pin5, n7432_2_pin8, n7432_2_pin9, n7432_2_pin10, n7432_2_pin11,
       n7486_1_pin3, n7486_1_pin9, n7486_1_pin11, n7486_2_pin3, n7486_2_pin11, n7486_3_pin3, n7486_3_pin9,
       n7486_3_pin11, n7486_4_pin3, n7486_4_pin11;

  _7486 #(.ShowInternalStructure("true")) u_7486_1 (
    .pin1(BIn[7]), .pin2(CIn[0]), .pin3(n7486_1_pin3), .pin4(n7486_1_pin3), .pin5(CarryIn), .pin6(SumOut[0]),
    .pin13(BIn[6]), .pin12(CIn[1]), .pin11(n7486_1_pin11), .pin10(n7486_1_pin11), .pin9(n7486_1_pin9),
    .pin8(SumOut[1]));
  _7408 #(.ShowInternalStructure("true")) u_7408_1 (
    .pin1(BIn[7]), .pin2(CIn[0]), .pin3(n7408_1_pin3), .pin4(n7486_1_pin3), .pin5(CarryIn),
    .pin6(n7408_1_pin6), .pin13(CIn[1]), .pin12(BIn[6]), .pin11(n7408_1_pin11), .pin10(n7486_1_pin11),
    .pin9(n7486_1_pin9), .pin8(n7408_1_pin8));
  _7432 #(.ShowInternalStructure("true")) u_7432_1 (
    .pin1(n7408_1_pin3), .pin2(n7408_1_pin6), .pin3(n7486_1_pin9), .pin4(n7432_1_pin4), .pin5(n7432_1_pin5),
    .pin6(n7432_1_pin6), .pin13(n7408_1_pin11), .pin12(n7408_1_pin8), .pin11(n7432_1_pin11),
    .pin10(n7432_1_pin10), .pin9(n7432_1_pin9), .pin8(n7432_1_pin8));
  _7486 #(.ShowInternalStructure("true")) u_7486_2 (
    .pin1(BIn[5]), .pin2(CIn[2]), .pin3(n7486_2_pin3), .pin4(n7486_2_pin3), .pin5(n7432_1_pin11),
    .pin6(SumOut[2]), .pin13(BIn[4]), .pin12(CIn[3]), .pin11(n7486_2_pin11), .pin10(n7486_2_pin11),
    .pin9(n7432_1_pin8), .pin8(SumOut[3]));
  _7408 #(.ShowInternalStructure("true")) u_7408_2 (
    .pin1(CIn[2]), .pin2(BIn[5]), .pin3(n7432_1_pin10), .pin4(n7486_2_pin3), .pin5(n7432_1_pin11),
    .pin6(n7432_1_pin9), .pin13(CIn[3]), .pin12(BIn[4]), .pin11(n7432_1_pin4), .pin10(n7432_1_pin8),
    .pin9(n7486_2_pin11), .pin8(n7432_1_pin5));
  _7486 #(.ShowInternalStructure("true")) u_7486_3 (
    .pin1(BIn[3]), .pin2(CIn[4]), .pin3(n7486_3_pin3), .pin4(n7486_3_pin3), .pin5(n7432_1_pin6),
    .pin6(SumOut[4]), .pin13(BIn[2]), .pin12(CIn[5]), .pin11(n7486_3_pin11), .pin10(n7486_3_pin11),
    .pin9(n7486_3_pin9), .pin8(SumOut[5]));
  _7408 #(.ShowInternalStructure("true")) u_7408_3 (
    .pin1(BIn[3]), .pin2(CIn[4]), .pin3(n7408_3_pin3), .pin4(n7486_3_pin3), .pin5(n7432_1_pin6),
    .pin6(n7408_3_pin6), .pin13(CIn[5]), .pin12(BIn[2]), .pin11(n7408_3_pin11), .pin10(n7486_3_pin11),
    .pin9(n7486_3_pin9), .pin8(n7408_3_pin8));
  _7432 #(.ShowInternalStructure("true")) u_7432_2 (
    .pin1(n7408_3_pin3), .pin2(n7408_3_pin6), .pin3(n7486_3_pin9), .pin4(n7432_2_pin4), .pin5(n7432_2_pin5),
    .pin6(CarryOut), .pin13(n7408_3_pin11), .pin12(n7408_3_pin8), .pin11(n7432_2_pin11),
    .pin10(n7432_2_pin10), .pin9(n7432_2_pin9), .pin8(n7432_2_pin8));
  _7486 #(.ShowInternalStructure("true")) u_7486_4 (
    .pin1(BIn[1]), .pin2(CIn[6]), .pin3(n7486_4_pin3), .pin4(n7486_4_pin3), .pin5(n7432_2_pin11),
    .pin6(SumOut[6]), .pin13(BIn[0]), .pin12(CIn[7]), .pin11(n7486_4_pin11), .pin10(n7486_4_pin11),
    .pin9(n7432_2_pin8), .pin8(SumOut[7]));
  _7408 #(.ShowInternalStructure("true")) u_7408_4 (
    .pin1(CIn[6]), .pin2(BIn[1]), .pin3(n7432_2_pin10), .pin4(n7486_4_pin3), .pin5(n7432_2_pin11),
    .pin6(n7432_2_pin9), .pin13(CIn[7]), .pin12(BIn[0]), .pin11(n7432_2_pin4), .pin10(n7432_2_pin8),
    .pin9(n7486_4_pin11), .pin8(n7432_2_pin5));
endmodule

// ALU
module ALU2 (
  input  [7:0] CIn,
  input  [7:0] BIn,
  input  UND,
  input  ODER,
  input  XODER,
  input  NICHT,
  output [7:0] SumOut
);

  wire n7404_1_pin2, n7404_1_pin8, n7404_1_pin10, n7404_1_pin12, n7432_1_pin3, n7432_1_pin6, n7432_1_pin8,
       n7432_1_pin11, n7486_1_pin3, n7486_1_pin6, n7486_1_pin8, n7486_1_pin11, n74245_1_pin11,
       n74245_1_pin12, n74245_1_pin13, n74245_1_pin14, n74245_1_pin15, n74245_1_pin16, n74245_1_pin17,
       n74245_1_pin18, n74245_2_pin11, n74245_2_pin12, n74245_2_pin13, n74245_2_pin14, n74245_3_pin11,
       n74245_3_pin12, n74245_3_pin13, n74245_3_pin14, n74245_4_pin11, n74245_4_pin12, n74245_4_pin13,
       n74245_4_pin14, n74245_4_pin15, n74245_4_pin16, n74245_4_pin17, n74245_4_pin18;

  _7404 #(.ShowInternalStructure("true")) u_7404_1 (
    .pin1(NICHT), .pin2(n7404_1_pin2), .pin13(UND), .pin12(n7404_1_pin12), .pin11(ODER),
    .pin10(n7404_1_pin10), .pin9(XODER), .pin8(n7404_1_pin8));  // open: pin3, pin4, pin5, pin6
  _74245 #(.ShowInternalStructure("true")) u_74245_1 (
    .pin2(SumOut[0]), .pin3(SumOut[1]), .pin4(SumOut[2]), .pin5(SumOut[3]), .pin6(SumOut[4]),
    .pin7(SumOut[5]), .pin8(SumOut[6]), .pin9(SumOut[7]), .pin19(n7404_1_pin12), .pin18(n74245_1_pin18),
    .pin17(n74245_1_pin17), .pin16(n74245_1_pin16), .pin15(n74245_1_pin15), .pin14(n74245_1_pin14),
    .pin13(n74245_1_pin13), .pin12(n74245_1_pin12), .pin11(n74245_1_pin11));  // open: pin1
  _7408 #(.ShowInternalStructure("true")) u_7408_1 (
    .pin1(CIn[0]), .pin2(BIn[0]), .pin3(n74245_1_pin18), .pin4(CIn[1]), .pin5(BIn[1]), .pin6(n74245_1_pin17),
    .pin13(CIn[2]), .pin12(BIn[2]), .pin11(n74245_1_pin16), .pin10(BIn[3]), .pin8(n74245_1_pin15));  // open: pin9
  _7408 #(.ShowInternalStructure("true")) u_7408_2 (
    .pin1(CIn[4]), .pin2(BIn[4]), .pin3(n74245_1_pin14), .pin4(CIn[5]), .pin5(BIn[5]), .pin6(n74245_1_pin13),
    .pin13(CIn[6]), .pin12(BIn[6]), .pin11(n74245_1_pin12), .pin10(CIn[7]), .pin9(BIn[7]),
    .pin8(n74245_1_pin11));
  Pull_Resistor pull_resistor_1 (.node(SumOut));
  _7432 #(.ShowInternalStructure("true")) u_7432_1 (
    .pin1(CIn[0]), .pin2(BIn[0]), .pin3(n7432_1_pin3), .pin4(CIn[1]), .pin5(BIn[1]), .pin6(n7432_1_pin6),
    .pin13(CIn[2]), .pin12(BIn[2]), .pin11(n7432_1_pin11), .pin10(CIn[3]), .pin9(BIn[3]), .pin8(n7432_1_pin8));
  _74245 #(.ShowInternalStructure("true")) u_74245_2 (
    .pin2(SumOut[0]), .pin3(SumOut[1]), .pin4(SumOut[2]), .pin5(SumOut[3]), .pin6(SumOut[4]),
    .pin7(SumOut[5]), .pin8(SumOut[6]), .pin9(SumOut[7]), .pin19(n7404_1_pin10), .pin18(n7432_1_pin3),
    .pin17(n7432_1_pin6), .pin16(n7432_1_pin11), .pin15(n7432_1_pin8), .pin14(n74245_2_pin14),
    .pin13(n74245_2_pin13), .pin12(n74245_2_pin12), .pin11(n74245_2_pin11));  // open: pin1
  _7432 #(.ShowInternalStructure("true")) u_7432_2 (
    .pin1(CIn[4]), .pin2(BIn[4]), .pin3(n74245_2_pin14), .pin4(CIn[5]), .pin5(BIn[5]), .pin6(n74245_2_pin13),
    .pin13(CIn[6]), .pin12(BIn[6]), .pin11(n74245_2_pin12), .pin10(CIn[7]), .pin9(BIn[7]),
    .pin8(n74245_2_pin11));
  _7486 #(.ShowInternalStructure("true")) u_7486_1 (
    .pin1(CIn[0]), .pin2(BIn[0]), .pin3(n7486_1_pin3), .pin4(CIn[1]), .pin5(BIn[1]), .pin6(n7486_1_pin6),
    .pin13(CIn[2]), .pin12(BIn[2]), .pin11(n7486_1_pin11), .pin10(CIn[3]), .pin9(BIn[3]), .pin8(n7486_1_pin8));
  _74245 #(.ShowInternalStructure("true")) u_74245_3 (
    .pin2(SumOut[0]), .pin3(SumOut[1]), .pin4(SumOut[2]), .pin5(SumOut[3]), .pin6(SumOut[4]),
    .pin7(SumOut[5]), .pin8(SumOut[6]), .pin9(SumOut[7]), .pin19(n7404_1_pin8), .pin18(n7486_1_pin3),
    .pin17(n7486_1_pin6), .pin16(n7486_1_pin11), .pin15(n7486_1_pin8), .pin14(n74245_3_pin14),
    .pin13(n74245_3_pin13), .pin12(n74245_3_pin12), .pin11(n74245_3_pin11));  // open: pin1
  _7486 #(.ShowInternalStructure("true")) u_7486_2 (
    .pin1(CIn[4]), .pin2(BIn[4]), .pin3(n74245_3_pin14), .pin4(CIn[5]), .pin5(BIn[5]), .pin6(n74245_3_pin13),
    .pin13(CIn[6]), .pin12(BIn[6]), .pin11(n74245_3_pin12), .pin10(CIn[7]), .pin9(BIn[7]),
    .pin8(n74245_3_pin11));
  _74245 #(.ShowInternalStructure("true")) u_74245_4 (
    .pin2(SumOut[0]), .pin3(SumOut[1]), .pin4(SumOut[2]), .pin5(SumOut[3]), .pin6(SumOut[4]),
    .pin7(SumOut[5]), .pin8(SumOut[6]), .pin9(SumOut[7]), .pin19(n7404_1_pin2), .pin18(n74245_4_pin18),
    .pin17(n74245_4_pin17), .pin16(n74245_4_pin16), .pin15(n74245_4_pin15), .pin14(n74245_4_pin14),
    .pin13(n74245_4_pin13), .pin12(n74245_4_pin12), .pin11(n74245_4_pin11));  // open: pin1
  _7404 #(.ShowInternalStructure("true")) u_7404_2 (
    .pin1(BIn[0]), .pin2(n74245_4_pin18), .pin3(BIn[1]), .pin4(n74245_4_pin17), .pin5(BIn[2]),
    .pin6(n74245_4_pin16), .pin13(BIn[3]), .pin12(n74245_4_pin15), .pin11(BIn[4]), .pin10(n74245_4_pin14),
    .pin9(BIn[5]), .pin8(n74245_4_pin13));
  _7404 #(.ShowInternalStructure("true")) u_7404_3 (
    .pin1(BIn[6]), .pin2(n74245_4_pin12), .pin3(BIn[7]), .pin4(n74245_4_pin11));  // open: pin5, pin6, pin13, pin12, pin11, pin10, pin9, pin8
endmodule

module ALU (
  input  [7:0] BIn,
  input  [7:0] CIn,
  input  [7:0] INSTR,
  input  [23:0] SQC,
  output A,
  output D,
  output [7:0] DOut,
  output Sign,
  output Zero,
  output Cry
);

  wire n7404_1_pin2, n7404_1_pin4, n7404_1_pin8, n7404_1_pin10, n7404_1_pin12, n7404_2_pin5, n7408_1_pin2,
       n7408_2_pin12, n7432_1_pin3, n7432_1_pin9, n7432_1_pin10, n7432_1_pin11, n7432_1_pin12, n7432_1_pin13,
       n7432_2_pin3, n7432_2_pin6, n7432_3_pin3, n7432_3_pin6, n7432_3_pin11, n7432_3_pin12, n7432_4_pin3,
       n7432_4_pin6, n7432_4_pin12, n74245_1_pin1, n74245_5_pin1, threetoeight_1_o_011, threetoeight_1_o_100,
       threetoeight_1_o_101, threetoeight_1_o_110, threetoeight_1_o_111;
  wire [2:0] n7408_1_pin8;
  wire [6:0] n74245_1_pin18;
  wire [7:0] alu1_1_sumout, alu1_2_sumout, alu2_1_sumout;

  _7408 #(.ShowInternalStructure("true")) u_7408_1 (
    .pin1(INSTR[1]), .pin2(n7408_1_pin2), .pin3(n7408_1_pin8[1]), .pin4(INSTR[2]), .pin5(n7408_1_pin2),
    .pin6(n7408_1_pin8[2]), .pin10(n7408_1_pin2), .pin9(INSTR[0]), .pin8(n7408_1_pin8[0]));  // open: pin13, pin12, pin11
  _7432 #(.ShowInternalStructure("true")) u_7432_1 (
    .pin1(SQC[7]), .pin2(SQC[8]), .pin3(n7432_1_pin3), .pin4(n7432_1_pin3), .pin5(SQC[9]),
    .pin6(n7408_1_pin2), .pin13(n7432_1_pin13), .pin12(n7432_1_pin12), .pin11(n7432_1_pin11),
    .pin10(n7432_1_pin10), .pin9(n7432_1_pin9), .pin8(n7432_1_pin12));
  _7408 #(.ShowInternalStructure("true")) u_7408_2 (
    .pin13(SQC[8]), .pin12(n7408_2_pin12), .pin11(A), .pin10(INSTR[3]), .pin9(SQC[8]), .pin8(D));  // open: pin1, pin2, pin3, pin4, pin5, pin6
  ThreeToEight threetoeight_1 (
    .FIn(n7408_1_pin8), .O_111(threetoeight_1_o_111), .O_110(threetoeight_1_o_110),
    .O_101(threetoeight_1_o_101), .O_100(threetoeight_1_o_100), .O_011(threetoeight_1_o_011),
    .O_010(n7432_1_pin9), .O_001(n7432_1_pin13));  // open: O_000
  _7432 #(.ShowInternalStructure("true")) u_7432_2 (
    .pin1(threetoeight_1_o_110), .pin2(threetoeight_1_o_101), .pin3(n7432_2_pin3),
    .pin4(threetoeight_1_o_100), .pin5(threetoeight_1_o_011), .pin6(n7432_2_pin6), .pin13(n7432_2_pin3),
    .pin12(n7432_2_pin6), .pin11(n7432_1_pin10));  // open: pin10, pin9, pin8
  _7404 #(.ShowInternalStructure("true")) u_7404_1 (
    .pin1(n7432_1_pin9), .pin2(n7404_1_pin2), .pin3(n7432_1_pin13), .pin4(n7404_1_pin4), .pin5(INSTR[3]),
    .pin6(n7408_2_pin12), .pin13(threetoeight_1_o_111), .pin12(n7404_1_pin12), .pin11(n7432_1_pin11),
    .pin10(n7404_1_pin10), .pin9(n7432_1_pin10), .pin8(n7404_1_pin8));
  ALU1 alu1_1 (
    .BIn({BIn[0], BIn[1], BIn[2], BIn[3], BIn[4], BIn[5], BIn[6], BIn[7]}), .CarryIn(n7432_1_pin9),
    .SumOut(alu1_1_sumout));  // open: CIn, CarryOut
  ALU1 alu1_2 (
    .BIn({BIn[0], BIn[1], BIn[2], BIn[3], BIn[4], BIn[5], BIn[6], BIn[7]}), .CIn(CIn), .CarryOut(Cry),
    .SumOut(alu1_2_sumout));  // open: CarryIn
  ALU2 alu2_1 (
    .CIn(CIn), .BIn({BIn[0], BIn[1], BIn[2], BIn[3], BIn[4], BIn[5], BIn[6], BIn[7]}),
    .UND(threetoeight_1_o_011), .ODER(threetoeight_1_o_100), .XODER(threetoeight_1_o_101),
    .NICHT(threetoeight_1_o_110), .SumOut(alu2_1_sumout));
  _7404 #(.ShowInternalStructure("true")) u_7404_2 (
    .pin5(n7404_2_pin5), .pin6(Zero));  // open: pin1, pin2, pin3, pin4, pin13, pin12, pin11, pin10, pin9, pin8
  _74245 #(.ShowInternalStructure("true")) u_74245_1 (
    .pin1(n74245_1_pin1), .pin2(BIn[0]), .pin3(BIn[7]), .pin4(BIn[6]), .pin5(BIn[5]), .pin6(BIn[4]),
    .pin7(BIn[3]), .pin8(BIn[2]), .pin9(BIn[1]), .pin19(n7404_1_pin12), .pin18(n74245_1_pin18[0]),
    .pin17(n74245_1_pin18[1]), .pin16(n74245_1_pin18[2]), .pin15(n74245_1_pin18[3]),
    .pin14(n74245_1_pin18[4]), .pin13(n74245_1_pin18[5]), .pin12(n74245_1_pin18[6]), .pin11(Sign));
  _74245 #(.ShowInternalStructure("true")) u_74245_2 (
    .pin1(n74245_1_pin1), .pin2(alu1_1_sumout[7]), .pin3(alu1_1_sumout[6]), .pin4(alu1_1_sumout[5]),
    .pin5(alu1_1_sumout[4]), .pin6(alu1_1_sumout[3]), .pin7(alu1_1_sumout[2]), .pin8(alu1_1_sumout[1]),
    .pin9(alu1_1_sumout[0]), .pin19(n7404_1_pin2), .pin18(n74245_1_pin18[0]), .pin17(n74245_1_pin18[1]),
    .pin16(n74245_1_pin18[2]), .pin15(n74245_1_pin18[3]), .pin14(n74245_1_pin18[4]),
    .pin13(n74245_1_pin18[5]), .pin12(n74245_1_pin18[6]), .pin11(Sign));
  _74245 #(.ShowInternalStructure("true")) u_74245_3 (
    .pin1(n74245_1_pin1), .pin2(alu1_2_sumout[0]), .pin3(alu1_2_sumout[1]), .pin4(alu1_2_sumout[2]),
    .pin5(alu1_2_sumout[3]), .pin6(alu1_2_sumout[4]), .pin7(alu1_2_sumout[5]), .pin8(alu1_2_sumout[6]),
    .pin9(alu1_2_sumout[7]), .pin19(n7404_1_pin4), .pin18(n74245_1_pin18[0]), .pin17(n74245_1_pin18[1]),
    .pin16(n74245_1_pin18[2]), .pin15(n74245_1_pin18[3]), .pin14(n74245_1_pin18[4]),
    .pin13(n74245_1_pin18[5]), .pin12(n74245_1_pin18[6]), .pin11(Sign));
  _74245 #(.ShowInternalStructure("true")) u_74245_4 (
    .pin1(n74245_1_pin1), .pin2(alu2_1_sumout[0]), .pin3(alu2_1_sumout[1]), .pin4(alu2_1_sumout[2]),
    .pin5(alu2_1_sumout[3]), .pin6(alu2_1_sumout[4]), .pin7(alu2_1_sumout[5]), .pin8(alu2_1_sumout[6]),
    .pin9(alu2_1_sumout[7]), .pin19(n7404_1_pin8), .pin18(n74245_1_pin18[0]), .pin17(n74245_1_pin18[1]),
    .pin16(n74245_1_pin18[2]), .pin15(n74245_1_pin18[3]), .pin14(n74245_1_pin18[4]),
    .pin13(n74245_1_pin18[5]), .pin12(n74245_1_pin18[6]), .pin11(Sign));
  Pull_Resistor pull_resistor_1 (.node({Sign, n74245_1_pin18}));
  _74245 #(.ShowInternalStructure("true")) u_74245_5 (
    .pin1(n74245_5_pin1), .pin2(n74245_1_pin18[0]), .pin3(n74245_1_pin18[1]), .pin4(n74245_1_pin18[2]),
    .pin5(n74245_1_pin18[3]), .pin6(n74245_1_pin18[4]), .pin7(n74245_1_pin18[5]), .pin8(n74245_1_pin18[6]),
    .pin9(Sign), .pin19(n7404_1_pin10), .pin18(DOut[0]), .pin17(DOut[1]), .pin16(DOut[2]), .pin15(DOut[3]),
    .pin14(DOut[4]), .pin13(DOut[5]), .pin12(DOut[6]), .pin11(DOut[7]));
  _7432 #(.ShowInternalStructure("true")) u_7432_3 (
    .pin1(n74245_1_pin18[0]), .pin2(n74245_1_pin18[1]), .pin3(n7432_3_pin3), .pin4(n7432_3_pin3),
    .pin5(n74245_1_pin18[2]), .pin6(n7432_3_pin6), .pin13(n74245_1_pin18[4]), .pin12(n7432_3_pin12),
    .pin11(n7432_3_pin11), .pin10(n74245_1_pin18[3]), .pin9(n7432_3_pin6), .pin8(n7432_3_pin12));
  _7432 #(.ShowInternalStructure("true")) u_7432_4 (
    .pin1(n74245_1_pin18[5]), .pin2(n7432_3_pin11), .pin3(n7432_4_pin3), .pin4(n7432_4_pin3),
    .pin5(n74245_1_pin18[6]), .pin6(n7432_4_pin6), .pin13(Sign), .pin12(n7432_4_pin12), .pin11(n7404_2_pin5),
    .pin9(n7432_4_pin6), .pin8(n7432_4_pin12));  // open: pin10
  // also tied to VCC on the sheet: {n74245_1_pin1, n74245_5_pin1}

  // Notes on the sheet:
  //   SQC: initial=0x1
endmodule

module ThreeToEight (
  input  [2:0] FIn,
  output O_111,
  output O_110,
  output O_101,
  output O_100,
  output O_011,
  output O_010,
  output O_001,
  output O_000
);

  wire n7404_1_pin6, n7404_1_pin8, n7404_1_pin10, n7404_1_pin12, n7404_2_pin4, n7404_2_pin6, n7404_2_pin8,
       n7404_2_pin10, n7404_2_pin12, n7411_1_pin5, n7411_1_pin10, n7411_2_pin9;

  _7411 #(.ShowInternalStructure("true")) u_7411_1 (
    .pin1(FIn[1]), .pin2(FIn[2]), .pin3(FIn[2]), .pin4(FIn[1]), .pin5(n7411_1_pin5), .pin6(O_110),
    .pin13(FIn[0]), .pin12(O_111), .pin11(FIn[0]), .pin10(n7411_1_pin10), .pin9(FIn[2]), .pin8(O_101));
  _7404 #(.ShowInternalStructure("true")) u_7404_1 (
    .pin1(FIn[0]), .pin2(n7411_1_pin5), .pin3(FIn[1]), .pin4(n7411_1_pin10), .pin5(FIn[1]),
    .pin6(n7404_1_pin6), .pin13(FIn[2]), .pin12(n7404_1_pin12), .pin11(FIn[2]), .pin10(n7404_1_pin10),
    .pin9(FIn[0]), .pin8(n7404_1_pin8));
  _7411 #(.ShowInternalStructure("true")) u_7411_2 (
    .pin1(n7404_1_pin6), .pin2(FIn[2]), .pin3(n7404_1_pin10), .pin4(FIn[1]), .pin5(FIn[0]), .pin6(O_011),
    .pin13(n7404_1_pin8), .pin12(O_100), .pin11(n7404_1_pin12), .pin10(FIn[1]), .pin9(n7411_2_pin9),
    .pin8(O_010));
  _7404 #(.ShowInternalStructure("true")) u_7404_2 (
    .pin1(FIn[0]), .pin2(n7411_2_pin9), .pin3(FIn[2]), .pin4(n7404_2_pin4), .pin5(FIn[1]),
    .pin6(n7404_2_pin6), .pin13(FIn[2]), .pin12(n7404_2_pin12), .pin11(FIn[1]), .pin10(n7404_2_pin10),
    .pin9(FIn[0]), .pin8(n7404_2_pin8));
  _7411 #(.ShowInternalStructure("true")) u_7411_3 (
    .pin1(n7404_2_pin6), .pin2(n7404_2_pin4), .pin13(FIn[0]), .pin12(O_001), .pin11(n7404_2_pin8),
    .pin10(n7404_2_pin10), .pin9(n7404_2_pin12), .pin8(O_000));  // open: pin3, pin4, pin5, pin6
endmodule

module Fetch (
  input  [23:0] SQC,
  output PCSEL,
  output MER,
  output LINC,
  output LINSTR,
  output INCSEL,
  output PCLOAD
);

  wire n7432_1_pin3, n7432_1_pin11;

  _7432 #(.ShowInternalStructure("true")) u_7432_1 (
    .pin1(SQC[0]), .pin2(SQC[1]), .pin3(n7432_1_pin3), .pin4(n7432_1_pin3), .pin5(SQC[2]), .pin6(MER),
    .pin13(SQC[0]), .pin12(SQC[1]), .pin11(n7432_1_pin11), .pin10(n7432_1_pin11), .pin9(SQC[2]), .pin8(PCSEL));
  _7432 #(.ShowInternalStructure("true")) u_7432_2 (
    .pin1(SQC[3]), .pin2(SQC[4]), .pin3(INCSEL), .pin13(SQC[1]), .pin12(SQC[1]), .pin11(LINSTR));  // open: pin4, pin5, pin6, pin10, pin9, pin8

  assign LINC = SQC[1];
  assign PCLOAD = SQC[3];
endmodule

module Dual_Register (
  input  [7:0] DIn,
  input  CLK,
  input  LOAD1,
  input  LOAD2,
  input  SELECT1,
  input  SELECT2,
  input  LOAD12,
  input  SELECT12,
  input  [15:0] D16In,
  output [7:0] DOut,
  output [15:0] D16Out
);

  wire n7404_1_pin2, n7404_1_pin4, n7404_1_pin6, n7404_1_pin8, n7404_1_pin12, n7432_1_pin1, n7432_1_pin2,
       n7432_1_pin3, n7432_1_pin5, n74245_1_pin1, n74245_1_pin19, n74245_2_pin1, n74245_3_pin1,
       n74245_4_pin1, n74245_5_pin1, n74245_6_pin1, n74245_7_pin1, n74245_8_pin1, n74273_1_pin11;
  wire [7:0] n74245_1_pin11, n74245_3_pin18, n74273_1_pin2, n74273_2_pin2;

  _74245 #(.ShowInternalStructure("true")) u_74245_1 (
    .pin1(n74245_1_pin1), .pin2(DIn[0]), .pin3(DIn[1]), .pin4(DIn[2]), .pin5(DIn[3]), .pin6(DIn[4]),
    .pin7(DIn[5]), .pin8(DIn[6]), .pin9(DIn[7]), .pin19(n74245_1_pin19), .pin18(n74245_1_pin11[7]),
    .pin17(n74245_1_pin11[6]), .pin16(n74245_1_pin11[5]), .pin15(n74245_1_pin11[4]),
    .pin14(n74245_1_pin11[3]), .pin13(n74245_1_pin11[2]), .pin12(n74245_1_pin11[1]), .pin11(n74245_1_pin11[0]));
  Pull_Resistor pull_resistor_1 (.node(n74245_1_pin11));
  _7404 #(.ShowInternalStructure("true")) u_7404_1 (
    .pin1(SELECT2), .pin2(n7404_1_pin2), .pin3(SELECT12), .pin4(n7404_1_pin4), .pin5(LOAD12),
    .pin6(n7404_1_pin6), .pin13(SELECT1), .pin12(n7404_1_pin12), .pin11(LOAD1), .pin10(n74245_1_pin19),
    .pin9(LOAD2), .pin8(n7404_1_pin8));
  _74245 #(.ShowInternalStructure("true")) u_74245_2 (
    .pin1(n74245_2_pin1), .pin2(D16In[0]), .pin3(D16In[1]), .pin4(D16In[2]), .pin5(D16In[3]),
    .pin6(D16In[4]), .pin7(D16In[5]), .pin8(D16In[6]), .pin9(D16In[7]), .pin19(n7404_1_pin6),
    .pin18(n74245_1_pin11[0]), .pin17(n74245_1_pin11[1]), .pin16(n74245_1_pin11[2]),
    .pin15(n74245_1_pin11[3]), .pin14(n74245_1_pin11[4]), .pin13(n74245_1_pin11[5]),
    .pin12(n74245_1_pin11[6]), .pin11(n74245_1_pin11[7]));
  _74245 #(.ShowInternalStructure("true")) u_74245_3 (
    .pin1(n74245_3_pin1), .pin2(D16In[8]), .pin3(D16In[9]), .pin4(D16In[10]), .pin5(D16In[11]),
    .pin6(D16In[12]), .pin7(D16In[13]), .pin8(D16In[14]), .pin9(D16In[15]), .pin19(n7404_1_pin6),
    .pin18(n74245_3_pin18[0]), .pin17(n74245_3_pin18[1]), .pin16(n74245_3_pin18[2]),
    .pin15(n74245_3_pin18[3]), .pin14(n74245_3_pin18[4]), .pin13(n74245_3_pin18[5]),
    .pin12(n74245_3_pin18[6]), .pin11(n74245_3_pin18[7]));
  _74273 #(.ShowInternalStructure("true")) u_74273_1 (
    .pin2(n74273_1_pin2[0]), .pin3(n74245_1_pin11[0]), .pin4(n74245_1_pin11[1]), .pin5(n74273_1_pin2[1]),
    .pin6(n74273_1_pin2[2]), .pin7(n74245_1_pin11[2]), .pin8(n74245_1_pin11[3]), .pin9(n74273_1_pin2[3]),
    .pin19(n74273_1_pin2[7]), .pin18(n74245_1_pin11[7]), .pin17(n74245_1_pin11[6]), .pin16(n74273_1_pin2[6]),
    .pin15(n74273_1_pin2[5]), .pin14(n74245_1_pin11[5]), .pin13(n74245_1_pin11[4]), .pin12(n74273_1_pin2[4]),
    .pin11(n74273_1_pin11));  // open: pin1
  _7432 #(.ShowInternalStructure("true")) u_7432_1 (
    .pin1(n7432_1_pin1), .pin2(n7432_1_pin2), .pin3(n7432_1_pin3), .pin4(n7432_1_pin2), .pin5(n7432_1_pin5),
    .pin6(n74273_1_pin11));  // open: pin13, pin12, pin11, pin10, pin9, pin8
  _7408 #(.ShowInternalStructure("true")) u_7408_1 (
    .pin1(LOAD1), .pin2(CLK), .pin3(n7432_1_pin5), .pin4(CLK), .pin5(LOAD2), .pin6(n7432_1_pin1),
    .pin13(LOAD12), .pin12(CLK), .pin11(n7432_1_pin2));  // open: pin10, pin9, pin8
  _74245 #(.ShowInternalStructure("true")) u_74245_4 (
    .pin1(n74245_4_pin1), .pin2(DIn[0]), .pin3(DIn[1]), .pin4(DIn[2]), .pin5(DIn[3]), .pin6(DIn[4]),
    .pin7(DIn[5]), .pin8(DIn[6]), .pin9(DIn[7]), .pin19(n7404_1_pin8), .pin18(n74245_3_pin18[0]),
    .pin17(n74245_3_pin18[1]), .pin16(n74245_3_pin18[2]), .pin15(n74245_3_pin18[3]),
    .pin14(n74245_3_pin18[4]), .pin13(n74245_3_pin18[5]), .pin12(n74245_3_pin18[6]), .pin11(n74245_3_pin18[7]));
  Pull_Resistor pull_resistor_2 (.node(n74245_3_pin18));
  _74273 #(.ShowInternalStructure("true")) u_74273_2 (
    .pin2(n74273_2_pin2[0]), .pin3(n74245_3_pin18[0]), .pin4(n74245_3_pin18[1]), .pin5(n74273_2_pin2[1]),
    .pin6(n74273_2_pin2[2]), .pin7(n74245_3_pin18[2]), .pin8(n74245_3_pin18[3]), .pin9(n74273_2_pin2[3]),
    .pin19(n74273_2_pin2[7]), .pin18(n74245_3_pin18[7]), .pin17(n74245_3_pin18[6]), .pin16(n74273_2_pin2[6]),
    .pin15(n74273_2_pin2[5]), .pin14(n74245_3_pin18[5]), .pin13(n74245_3_pin18[4]), .pin12(n74273_2_pin2[4]),
    .pin11(n7432_1_pin3));  // open: pin1
  _74245 #(.ShowInternalStructure("true")) u_74245_5 (
    .pin1(n74245_5_pin1), .pin2(n74273_1_pin2[7]), .pin3(n74273_1_pin2[6]), .pin4(n74273_1_pin2[5]),
    .pin5(n74273_1_pin2[4]), .pin6(n74273_1_pin2[3]), .pin7(n74273_1_pin2[2]), .pin8(n74273_1_pin2[1]),
    .pin9(n74273_1_pin2[0]), .pin19(n7404_1_pin12), .pin18(DOut[7]), .pin17(DOut[6]), .pin16(DOut[5]),
    .pin15(DOut[4]), .pin14(DOut[3]), .pin13(DOut[2]), .pin12(DOut[1]), .pin11(DOut[0]));
  _74245 #(.ShowInternalStructure("true")) u_74245_6 (
    .pin1(n74245_6_pin1), .pin2(n74273_2_pin2[7]), .pin3(n74273_2_pin2[6]), .pin4(n74273_2_pin2[5]),
    .pin5(n74273_2_pin2[4]), .pin6(n74273_2_pin2[3]), .pin7(n74273_2_pin2[2]), .pin8(n74273_2_pin2[1]),
    .pin9(n74273_2_pin2[0]), .pin19(n7404_1_pin2), .pin18(DOut[7]), .pin17(DOut[6]), .pin16(DOut[5]),
    .pin15(DOut[4]), .pin14(DOut[3]), .pin13(DOut[2]), .pin12(DOut[1]), .pin11(DOut[0]));
  _74245 #(.ShowInternalStructure("true")) u_74245_7 (
    .pin1(n74245_7_pin1), .pin2(n74273_1_pin2[0]), .pin3(n74273_1_pin2[1]), .pin4(n74273_1_pin2[2]),
    .pin5(n74273_1_pin2[3]), .pin6(n74273_1_pin2[4]), .pin7(n74273_1_pin2[5]), .pin8(n74273_1_pin2[6]),
    .pin9(n74273_1_pin2[7]), .pin19(n7404_1_pin4), .pin18(D16Out[7]), .pin17(D16Out[6]), .pin16(D16Out[5]),
    .pin15(D16Out[4]), .pin14(D16Out[3]), .pin13(D16Out[2]), .pin12(D16Out[1]), .pin11(D16Out[0]));
  _74245 #(.ShowInternalStructure("true")) u_74245_8 (
    .pin1(n74245_8_pin1), .pin2(n74273_2_pin2[0]), .pin3(n74273_2_pin2[1]), .pin4(n74273_2_pin2[2]),
    .pin5(n74273_2_pin2[3]), .pin6(n74273_2_pin2[4]), .pin7(n74273_2_pin2[5]), .pin8(n74273_2_pin2[6]),
    .pin9(n74273_2_pin2[7]), .pin19(n7404_1_pin4), .pin18(D16Out[8]), .pin17(D16Out[9]), .pin16(D16Out[10]),
    .pin15(D16Out[11]), .pin14(D16Out[12]), .pin13(D16Out[13]), .pin12(D16Out[14]), .pin11(D16Out[15]));
  // also tied to VCC on the sheet: {n74245_1_pin1, n74245_2_pin1, n74245_3_pin1, n74245_4_pin1, n74245_5_pin1, n74245_6_pin1, n74245_7_pin1, n74245_8_pin1}
endmodule

module Dual_Regist_B_C (
  input  [7:0] DIn,
  input  CLK,
  input  LOAD1,
  input  LOAD2,
  input  SELECT1,
  input  SELECT2,
  input  LOAD12,
  input  SELECT12,
  input  [15:0] D16In,
  output [7:0] BOut,
  output [7:0] COut,
  output [15:0] D16Out
);

  wire n7404_1_pin4, n7404_1_pin6, n7404_1_pin8, n7432_1_pin1, n7432_1_pin2, n7432_1_pin3, n7432_1_pin5,
       n74245_1_pin1, n74245_1_pin19, n74245_2_pin1, n74245_3_pin1, n74245_4_pin1, n74245_5_pin1,
       n74245_6_pin1, n74273_1_pin11;
  wire [7:0] n74245_1_pin18, n74245_3_pin18;

  _74245 #(.ShowInternalStructure("true")) u_74245_1 (
    .pin1(n74245_1_pin1), .pin2(DIn[0]), .pin3(DIn[1]), .pin4(DIn[2]), .pin5(DIn[3]), .pin6(DIn[4]),
    .pin7(DIn[5]), .pin8(DIn[6]), .pin9(DIn[7]), .pin19(n74245_1_pin19), .pin18(n74245_1_pin18[0]),
    .pin17(n74245_1_pin18[1]), .pin16(n74245_1_pin18[2]), .pin15(n74245_1_pin18[3]),
    .pin14(n74245_1_pin18[4]), .pin13(n74245_1_pin18[5]), .pin12(n74245_1_pin18[6]), .pin11(n74245_1_pin18[7]));
  Pull_Resistor pull_resistor_1 (.node(n74245_1_pin18));
  _7404 #(.ShowInternalStructure("true")) u_7404_1 (
    .pin1(SELECT2), .pin3(SELECT12), .pin4(n7404_1_pin4), .pin5(LOAD12), .pin6(n7404_1_pin6),
    .pin13(SELECT1), .pin11(LOAD1), .pin10(n74245_1_pin19), .pin9(LOAD2), .pin8(n7404_1_pin8));  // open: pin2, pin12
  _74245 #(.ShowInternalStructure("true")) u_74245_2 (
    .pin1(n74245_2_pin1), .pin2(D16In[7]), .pin3(D16In[6]), .pin4(D16In[5]), .pin5(D16In[4]),
    .pin6(D16In[3]), .pin7(D16In[2]), .pin8(D16In[1]), .pin9(D16In[0]), .pin19(n7404_1_pin6),
    .pin18(n74245_1_pin18[0]), .pin17(n74245_1_pin18[1]), .pin16(n74245_1_pin18[2]),
    .pin15(n74245_1_pin18[3]), .pin14(n74245_1_pin18[4]), .pin13(n74245_1_pin18[5]),
    .pin12(n74245_1_pin18[6]), .pin11(n74245_1_pin18[7]));
  _74245 #(.ShowInternalStructure("true")) u_74245_3 (
    .pin1(n74245_3_pin1), .pin2(D16In[15]), .pin3(D16In[14]), .pin4(D16In[13]), .pin5(D16In[12]),
    .pin6(D16In[11]), .pin7(D16In[10]), .pin8(D16In[9]), .pin9(D16In[8]), .pin19(n7404_1_pin6),
    .pin18(n74245_3_pin18[0]), .pin17(n74245_3_pin18[1]), .pin16(n74245_3_pin18[2]),
    .pin15(n74245_3_pin18[3]), .pin14(n74245_3_pin18[4]), .pin13(n74245_3_pin18[5]),
    .pin12(n74245_3_pin18[6]), .pin11(n74245_3_pin18[7]));
  _74273 #(.ShowInternalStructure("true")) u_74273_1 (
    .pin2(BOut[0]), .pin3(n74245_1_pin18[0]), .pin4(n74245_1_pin18[1]), .pin5(BOut[1]), .pin6(BOut[2]),
    .pin7(n74245_1_pin18[2]), .pin8(n74245_1_pin18[3]), .pin9(BOut[3]), .pin19(BOut[7]),
    .pin18(n74245_1_pin18[7]), .pin17(n74245_1_pin18[6]), .pin16(BOut[6]), .pin15(BOut[5]),
    .pin14(n74245_1_pin18[5]), .pin13(n74245_1_pin18[4]), .pin12(BOut[4]), .pin11(n74273_1_pin11));  // open: pin1
  _7432 #(.ShowInternalStructure("true")) u_7432_1 (
    .pin1(n7432_1_pin1), .pin2(n7432_1_pin2), .pin3(n7432_1_pin3), .pin4(n7432_1_pin2), .pin5(n7432_1_pin5),
    .pin6(n74273_1_pin11));  // open: pin13, pin12, pin11, pin10, pin9, pin8
  _7408 #(.ShowInternalStructure("true")) u_7408_1 (
    .pin1(LOAD1), .pin2(CLK), .pin3(n7432_1_pin5), .pin4(CLK), .pin5(LOAD2), .pin6(n7432_1_pin1),
    .pin13(LOAD12), .pin12(CLK), .pin11(n7432_1_pin2));  // open: pin10, pin9, pin8
  _74245 #(.ShowInternalStructure("true")) u_74245_4 (
    .pin1(n74245_4_pin1), .pin2(DIn[0]), .pin3(DIn[1]), .pin4(DIn[2]), .pin5(DIn[3]), .pin6(DIn[4]),
    .pin7(DIn[5]), .pin8(DIn[6]), .pin9(DIn[7]), .pin19(n7404_1_pin8), .pin18(n74245_3_pin18[0]),
    .pin17(n74245_3_pin18[1]), .pin16(n74245_3_pin18[2]), .pin15(n74245_3_pin18[3]),
    .pin14(n74245_3_pin18[4]), .pin13(n74245_3_pin18[5]), .pin12(n74245_3_pin18[6]), .pin11(n74245_3_pin18[7]));
  Pull_Resistor pull_resistor_2 (.node(n74245_3_pin18));
  _74273 #(.ShowInternalStructure("true")) u_74273_2 (
    .pin2(COut[0]), .pin3(n74245_3_pin18[0]), .pin4(n74245_3_pin18[1]), .pin5(COut[1]), .pin6(COut[2]),
    .pin7(n74245_3_pin18[2]), .pin8(n74245_3_pin18[3]), .pin9(COut[3]), .pin19(COut[7]),
    .pin18(n74245_3_pin18[7]), .pin17(n74245_3_pin18[6]), .pin16(COut[6]), .pin15(COut[5]),
    .pin14(n74245_3_pin18[5]), .pin13(n74245_3_pin18[4]), .pin12(COut[4]), .pin11(n7432_1_pin3));  // open: pin1
  _74245 #(.ShowInternalStructure("true")) u_74245_5 (
    .pin1(n74245_5_pin1), .pin2(BOut[7]), .pin3(BOut[6]), .pin4(BOut[5]), .pin5(BOut[4]), .pin6(BOut[3]),
    .pin7(BOut[2]), .pin8(BOut[1]), .pin9(BOut[0]), .pin19(n7404_1_pin4), .pin18(D16Out[0]),
    .pin17(D16Out[1]), .pin16(D16Out[2]), .pin15(D16Out[3]), .pin14(D16Out[4]), .pin13(D16Out[5]),
    .pin12(D16Out[6]), .pin11(D16Out[7]));
  _74245 #(.ShowInternalStructure("true")) u_74245_6 (
    .pin1(n74245_6_pin1), .pin2(COut[0]), .pin3(COut[1]), .pin4(COut[2]), .pin5(COut[3]), .pin6(COut[4]),
    .pin7(COut[5]), .pin8(COut[6]), .pin9(COut[7]), .pin19(n7404_1_pin4), .pin18(D16Out[8]),
    .pin17(D16Out[9]), .pin16(D16Out[10]), .pin15(D16Out[11]), .pin14(D16Out[12]), .pin13(D16Out[13]),
    .pin12(D16Out[14]), .pin11(D16Out[15]));
  // also tied to VCC on the sheet: {n74245_1_pin1, n74245_2_pin1, n74245_3_pin1, n74245_4_pin1, n74245_5_pin1, n74245_6_pin1}
endmodule

module Incrementer (
  input  CLK,
  input  LoadINC,
  input  [15:0] AIn,
  input  SELECTINC,
  output [15:0] AOut
);

  wire alu1_1_carryout, n7404_1_pin2, n74245_1_pin1, n74245_2_pin1;
  wire [7:0] alu1_1_sumout, alu1_2_sumout, dual_regist_b_c_1_bout, dual_regist_b_c_1_cout,
       pull_resistor_1_node, pull_resistor_2_node;

  _7404 #(.ShowInternalStructure("true")) u_7404_1 (
    .pin1(SELECTINC), .pin2(n7404_1_pin2));  // open: pin3, pin4, pin5, pin6, pin13, pin12, pin11, pin10, pin9, pin8
  Dual_Regist_B_C dual_regist_b_c_1 (
    .CLK(CLK), .LOAD12(LoadINC), .D16In(AIn), .BOut(dual_regist_b_c_1_bout), .COut(dual_regist_b_c_1_cout));  // open: DIn, LOAD1, LOAD2, SELECT1, SELECT2, SELECT12, D16Out
  Pull_Resistor pull_resistor_1 (.node(pull_resistor_1_node));
  Pull_Resistor pull_resistor_2 (.node(pull_resistor_2_node));
  ALU1 alu1_1 (
    .BIn(dual_regist_b_c_1_bout), .CarryIn(1'b1), .CIn(pull_resistor_1_node), .CarryOut(alu1_1_carryout),
    .SumOut(alu1_1_sumout));
  ALU1 alu1_2 (
    .BIn(dual_regist_b_c_1_cout), .CarryIn(alu1_1_carryout), .CIn(pull_resistor_2_node),
    .SumOut(alu1_2_sumout));  // open: CarryOut
  _74245 #(.ShowInternalStructure("true")) u_74245_1 (
    .pin1(n74245_1_pin1), .pin2(alu1_1_sumout[0]), .pin3(alu1_1_sumout[1]), .pin4(alu1_1_sumout[2]),
    .pin5(alu1_1_sumout[3]), .pin6(alu1_1_sumout[4]), .pin7(alu1_1_sumout[5]), .pin8(alu1_1_sumout[6]),
    .pin9(alu1_1_sumout[7]), .pin19(n7404_1_pin2), .pin18(AOut[0]), .pin17(AOut[1]), .pin16(AOut[2]),
    .pin15(AOut[3]), .pin14(AOut[4]), .pin13(AOut[5]), .pin12(AOut[6]), .pin11(AOut[7]));
  _74245 #(.ShowInternalStructure("true")) u_74245_2 (
    .pin1(n74245_2_pin1), .pin2(alu1_2_sumout[0]), .pin3(alu1_2_sumout[1]), .pin4(alu1_2_sumout[2]),
    .pin5(alu1_2_sumout[3]), .pin6(alu1_2_sumout[4]), .pin7(alu1_2_sumout[5]), .pin8(alu1_2_sumout[6]),
    .pin9(alu1_2_sumout[7]), .pin19(n7404_1_pin2), .pin18(AOut[8]), .pin17(AOut[9]), .pin16(AOut[10]),
    .pin15(AOut[11]), .pin14(AOut[12]), .pin13(AOut[13]), .pin12(AOut[14]), .pin11(AOut[15]));
  // also tied to VCC on the sheet: {n74245_1_pin1, n74245_2_pin1}
endmodule

module Instr_Decoder (
  input  [7:0] in_1,
  output setab,
  output mov8,
  output goto,
  output alu,
  output load,
  output store,
  output mov16,
  output OUT_8,
  output HALT,
  output inc
);

  wire n7404_1_pin2, n7404_1_pin4, n7404_1_pin6, n7404_1_pin8, n7404_1_pin10, n7404_1_pin12, n7404_2_pin2,
       n7404_2_pin4, n7408_1_pin6, n7408_2_pin3, n7408_2_pin6, n7408_2_pin11, n7408_3_pin3, n7408_3_pin6,
       n7408_3_pin8, n7408_3_pin11, n7408_4_pin3, n7408_4_pin6, n7408_4_pin8, n7408_4_pin11, n7408_5_pin3,
       n7408_5_pin5, n7408_5_pin11, n7408_6_pin1, n7408_7_pin3, n7408_7_pin6, n7408_7_pin8, n7408_7_pin11,
       n7408_8_pin1, n7408_8_pin3, n7408_8_pin11, n7408_9_pin3, n7408_9_pin11, n7408_10_pin2, n7408_10_pin3,
       n7408_10_pin11, n7408_11_pin1, n7408_11_pin3, n7408_11_pin11;

  _7404 #(.ShowInternalStructure("true")) u_7404_1 (
    .pin1(in_1[7]), .pin2(n7404_1_pin2), .pin3(in_1[6]), .pin4(n7404_1_pin4), .pin5(in_1[5]),
    .pin6(n7404_1_pin6), .pin13(in_1[4]), .pin12(n7404_1_pin12), .pin11(in_1[3]), .pin10(n7404_1_pin10),
    .pin9(in_1[2]), .pin8(n7404_1_pin8));
  _7404 #(.ShowInternalStructure("true")) u_7404_2 (
    .pin1(in_1[0]), .pin2(n7404_2_pin2), .pin3(in_1[1]), .pin4(n7404_2_pin4), .pin11(n7404_2_pin4));  // open: pin5, pin6, pin13, pin12, pin10, pin9, pin8
  _7408 #(.ShowInternalStructure("true")) u_7408_1 (
    .pin1(n7404_1_pin2), .pin2(in_1[6]), .pin3(setab), .pin4(n7404_1_pin4), .pin5(in_1[7]),
    .pin6(n7408_1_pin6), .pin13(n7404_1_pin2), .pin12(n7404_1_pin4), .pin11(mov8), .pin10(in_1[7]),
    .pin9(in_1[6]), .pin8(goto));
  _7408 #(.ShowInternalStructure("true")) u_7408_2 (
    .pin1(in_1[7]), .pin2(n7404_1_pin4), .pin3(n7408_2_pin3), .pin4(n7408_2_pin3), .pin5(n7404_1_pin6),
    .pin6(n7408_2_pin6), .pin13(n7408_1_pin6), .pin12(n7404_1_pin6), .pin11(n7408_2_pin11),
    .pin10(n7408_2_pin11), .pin9(n7404_1_pin12), .pin8(alu));
  _7408 #(.ShowInternalStructure("true")) u_7408_3 (
    .pin1(n7408_2_pin6), .pin2(in_1[4]), .pin3(n7408_3_pin3), .pin4(n7408_3_pin3), .pin5(n7404_1_pin10),
    .pin6(n7408_3_pin6), .pin13(in_1[7]), .pin12(n7404_1_pin4), .pin11(n7408_3_pin11), .pin10(n7408_3_pin11),
    .pin9(n7404_1_pin6), .pin8(n7408_3_pin8));
  _7408 #(.ShowInternalStructure("true")) u_7408_4 (
    .pin1(in_1[7]), .pin2(n7404_1_pin4), .pin3(n7408_4_pin3), .pin4(n7408_4_pin3), .pin5(in_1[5]),
    .pin6(n7408_4_pin6), .pin13(n7408_3_pin8), .pin12(in_1[4]), .pin11(n7408_4_pin11), .pin10(n7408_4_pin11),
    .pin9(in_1[3]), .pin8(n7408_4_pin8));
  _7408 #(.ShowInternalStructure("true")) u_7408_5 (
    .pin1(n7404_1_pin10), .pin2(n7404_1_pin10), .pin3(n7408_5_pin3), .pin4(n7408_5_pin3),
    .pin5(n7408_5_pin5), .pin6(mov16), .pin13(n7404_1_pin10), .pin12(n7408_3_pin6), .pin11(n7408_5_pin11),
    .pin10(n7404_1_pin8), .pin9(n7408_4_pin8), .pin8(store));
  _7408 #(.ShowInternalStructure("true")) u_7408_6 (
    .pin1(n7408_6_pin1), .pin2(n7404_2_pin4), .pin3(OUT_8), .pin13(n7404_1_pin8), .pin12(n7408_5_pin11),
    .pin11(load));  // open: pin4, pin5, pin6, pin10, pin9, pin8
  _7408 #(.ShowInternalStructure("true")) u_7408_7 (
    .pin1(n7408_4_pin6), .pin2(in_1[4]), .pin3(n7408_7_pin3), .pin4(n7408_7_pin3), .pin5(n7404_1_pin10),
    .pin6(n7408_7_pin6), .pin13(in_1[7]), .pin12(n7404_1_pin4), .pin11(n7408_7_pin11), .pin10(n7408_7_pin11),
    .pin9(in_1[5]), .pin8(n7408_7_pin8));
  _7408 #(.ShowInternalStructure("true")) u_7408_8 (
    .pin1(n7408_8_pin1), .pin2(n7404_2_pin2), .pin3(n7408_8_pin3), .pin4(n7408_8_pin3), .pin5(n7404_2_pin4),
    .pin6(inc), .pin13(n7408_7_pin6), .pin12(n7404_1_pin10), .pin11(n7408_8_pin11), .pin10(n7408_8_pin11),
    .pin9(n7404_1_pin8), .pin8(n7408_8_pin1));
  _7408 #(.ShowInternalStructure("true")) u_7408_9 (
    .pin1(in_1[7]), .pin2(n7404_1_pin4), .pin3(n7408_9_pin3), .pin4(n7408_9_pin3), .pin5(in_1[5]),
    .pin13(n7408_7_pin8), .pin12(n7404_1_pin12), .pin11(n7408_9_pin11), .pin10(n7408_9_pin11),
    .pin9(n7404_1_pin4), .pin8(n7408_5_pin5));  // open: pin6
  _7408 #(.ShowInternalStructure("true")) u_7408_10 (
    .pin1(n7404_1_pin10), .pin2(n7408_10_pin2), .pin3(n7408_10_pin3), .pin4(n7408_10_pin3), .pin5(in_1[2]),
    .pin6(n7408_6_pin1), .pin13(in_1[7]), .pin12(n7404_1_pin4), .pin11(n7408_10_pin11),
    .pin10(n7408_10_pin11), .pin9(n7404_1_pin6), .pin8(n7408_10_pin2));
  _7408 #(.ShowInternalStructure("true")) u_7408_11 (
    .pin1(n7408_11_pin1), .pin2(in_1[2]), .pin3(n7408_11_pin3), .pin4(n7408_11_pin3), .pin5(n7404_2_pin4),
    .pin6(HALT), .pin13(n7408_10_pin2), .pin12(in_1[4]), .pin11(n7408_11_pin11), .pin10(n7408_11_pin11),
    .pin9(in_1[3]), .pin8(n7408_11_pin1));
  _7408 #(.ShowInternalStructure("true")) u_7408_12 ();  // open: pin1, pin2, pin3, pin4, pin5, pin6, pin13, pin12, pin11, pin10, pin9, pin8
endmodule

module MOV8 (
  input  [23:0] SQC,
  input  [7:0] INSTR,
  output [7:0] LOAD,
  output [7:0] SEL
);

  wire n7404_1_pin2, n7404_1_pin4, n7432_1_pin8, n7432_1_pin11, n74245_1_pin1, n74245_2_pin1;
  wire [7:0] threetoeight_1_o_000, threetoeight_2_o_111;

  _7432 #(.ShowInternalStructure("true")) u_7432_1 (
    .pin13(SQC[7]), .pin12(SQC[6]), .pin11(n7432_1_pin11), .pin10(n7432_1_pin11), .pin9(SQC[5]),
    .pin8(n7432_1_pin8));  // open: pin1, pin2, pin3, pin4, pin5, pin6
  _7404 #(.ShowInternalStructure("true")) u_7404_1 (
    .pin1(SQC[6]), .pin2(n7404_1_pin2), .pin3(n7432_1_pin8), .pin4(n7404_1_pin4));  // open: pin5, pin6, pin13, pin12, pin11, pin10, pin9, pin8
  ThreeToEight threetoeight_1 (
    .FIn({INSTR[3], INSTR[4], INSTR[5]}), .O_111(threetoeight_1_o_000[7]), .O_110(threetoeight_1_o_000[6]),
    .O_101(threetoeight_1_o_000[5]), .O_100(threetoeight_1_o_000[4]), .O_011(threetoeight_1_o_000[3]),
    .O_010(threetoeight_1_o_000[2]), .O_001(threetoeight_1_o_000[1]), .O_000(threetoeight_1_o_000[0]));
  ThreeToEight threetoeight_2 (
    .FIn(INSTR[2:0]), .O_111(threetoeight_2_o_111[0]), .O_110(threetoeight_2_o_111[1]),
    .O_101(threetoeight_2_o_111[2]), .O_100(threetoeight_2_o_111[3]), .O_011(threetoeight_2_o_111[4]),
    .O_010(threetoeight_2_o_111[5]), .O_001(threetoeight_2_o_111[6]), .O_000(threetoeight_2_o_111[7]));
  _74245 #(.ShowInternalStructure("true")) u_74245_1 (
    .pin1(n74245_1_pin1), .pin2(threetoeight_1_o_000[0]), .pin3(threetoeight_1_o_000[1]),
    .pin4(threetoeight_1_o_000[2]), .pin5(threetoeight_1_o_000[3]), .pin6(threetoeight_1_o_000[4]),
    .pin7(threetoeight_1_o_000[5]), .pin8(threetoeight_1_o_000[6]), .pin9(threetoeight_1_o_000[7]),
    .pin19(n7404_1_pin2), .pin18(SEL[0]), .pin17(SEL[1]), .pin16(SEL[2]), .pin15(SEL[3]), .pin14(SEL[4]),
    .pin13(SEL[5]), .pin12(SEL[6]), .pin11(SEL[7]));
  _74245 #(.ShowInternalStructure("true")) u_74245_2 (
    .pin1(n74245_2_pin1), .pin2(threetoeight_2_o_111[7]), .pin3(threetoeight_2_o_111[6]),
    .pin4(threetoeight_2_o_111[5]), .pin5(threetoeight_2_o_111[4]), .pin6(threetoeight_2_o_111[3]),
    .pin7(threetoeight_2_o_111[2]), .pin8(threetoeight_2_o_111[1]), .pin9(threetoeight_2_o_111[0]),
    .pin19(n7404_1_pin4), .pin18(LOAD[7]), .pin17(LOAD[6]), .pin16(LOAD[5]), .pin15(LOAD[4]),
    .pin14(LOAD[3]), .pin13(LOAD[2]), .pin12(LOAD[1]), .pin11(LOAD[0]));
  Pull_Resistor pull_resistor_1 (.node(SEL));
  Pull_Resistor pull_resistor_2 (.node(LOAD));
  // also tied to VCC on the sheet: {n74245_1_pin1, n74245_2_pin1}
endmodule

module INSTRUCTIONS (
  input  MOV_8,
  input  [23:0] SQC,
  input  [7:0] INSTR,
  input  LOAD_8,
  input  [2:0] F,
  input  SAVE_8,
  input  SET_AB,
  input  GOTO_16,
  input  [7:0] REG_IN,
  output [7:0] REG_SELECT,
  output [7:0] REG_LOAD,
  output M_SEL,
  output PC_SEL,
  output MEW,
  output MER,
  output ALOAD,
  output BLOAD,
  output [7:0] DOut,
  output J1_LOAD,
  output M1_LOAD,
  output J2_LOAD,
  output M2_LOAD,
  output INC_LOAD,
  output J_SEL,
  output PC_LOAD,
  output INC_SEL,
  output AT_08
);

  wire goto_1_mer, goto_1_msel, goto_1_pcsel, load_1_mer, load_1_msel, load_1_pcsel, n7432_1_pin3,
       n7432_1_pin11, save_1_msel, save_1_pcsel;
  wire [7:0] gate_8_1_dout, gate_8_2_dout, gate_8_3_dout, gate_8_4_dout, gate_8_5_dout, gate_8_6_dout,
       gate_8_7_dout, gate_8_8_dout, gate_8_9_dout, load_1_reg_load, mov8_1_load, mov8_1_sel, or_8_2_out_1,
       save_1_reg_select;
  wire [23:0] gate_24_1_dout, gate_24_2_dout, gate_24_3_dout, gate_24_4_dout, gate_24_5_dout;

  GATE_24 gate_24_1 (.EN(MOV_8), .DIn(SQC), .DOut(gate_24_1_dout));
  GATE_24 gate_24_2 (.EN(LOAD_8), .DIn(SQC), .DOut(gate_24_2_dout));
  GATE_24 gate_24_3 (.EN(SAVE_8), .DIn(SQC), .DOut(gate_24_3_dout));
  GATE_24 gate_24_4 (.EN(SET_AB), .DIn(SQC), .DOut(gate_24_4_dout));
  GATE_24 gate_24_5 (.EN(GOTO_16), .DIn(SQC), .DOut(gate_24_5_dout));
  GATE_8 gate_8_1 (.EN(MOV_8), .DIn(INSTR), .DOut(gate_8_1_dout));
  GATE_8 gate_8_2 (.EN(LOAD_8), .DIn(INSTR), .DOut(gate_8_2_dout));
  GATE_8 gate_8_3 (.EN(SAVE_8), .DIn(INSTR), .DOut(gate_8_3_dout));
  GATE_8 gate_8_4 (.EN(SET_AB), .DIn(INSTR), .DOut(gate_8_4_dout));
  GATE_8 gate_8_5 (.EN(GOTO_16), .DIn(INSTR), .DOut(gate_8_5_dout));
  Pull_Resistor pull_resistor_1 (.node(gate_24_1_dout));
  Pull_Resistor pull_resistor_2 (.node(gate_8_1_dout));
  Pull_Resistor pull_resistor_3 (.node(gate_24_2_dout));
  Pull_Resistor pull_resistor_4 (.node(gate_24_3_dout));
  Pull_Resistor pull_resistor_5 (.node(gate_24_4_dout));
  Pull_Resistor pull_resistor_6 (.node(gate_24_5_dout));
  MOV8 mov8_1 (.SQC(gate_24_1_dout), .INSTR(gate_8_1_dout), .LOAD(mov8_1_load), .SEL(mov8_1_sel));
  LOAD load_1 (
    .INST(gate_8_2_dout), .SQC(gate_24_2_dout), .REG_LOAD(load_1_reg_load), .MSEL(load_1_msel),
    .PCSEL(load_1_pcsel), .MER(load_1_mer));
  SAVE save_1 (
    .INSTR(gate_8_3_dout), .SQC(gate_24_3_dout), .REG_SELECT(save_1_reg_select), .MSEL(save_1_msel),
    .PCSEL(save_1_pcsel), .MEW(MEW));
  setab setab_1 (.INSTR(gate_8_4_dout), .SQC(gate_24_4_dout), .A_LOAD(ALOAD), .B_LOAD(BLOAD), .DOut(DOut));
  GOTO goto_1 (
    .INSTR(gate_8_5_dout), .COND_REG(F), .SQC(gate_24_5_dout), .J1LOAD(J1_LOAD), .M1LOAD(M1_LOAD),
    .J2LOAD(J2_LOAD), .M2LOAD(M2_LOAD), .MER(goto_1_mer), .INCLOAD(INC_LOAD), .JSEL(J_SEL),
    .MSEL(goto_1_msel), .PCSEL(goto_1_pcsel), .PCLOAD(PC_LOAD), .INCSEL(INC_SEL));
  _7432 #(.ShowInternalStructure("true")) u_7432_1 (
    .pin1(load_1_msel), .pin2(save_1_msel), .pin3(n7432_1_pin3), .pin4(n7432_1_pin3), .pin5(goto_1_msel),
    .pin6(M_SEL), .pin13(load_1_pcsel), .pin12(save_1_pcsel), .pin11(n7432_1_pin11), .pin10(n7432_1_pin11),
    .pin9(goto_1_pcsel), .pin8(PC_SEL));
  _7432 #(.ShowInternalStructure("true")) u_7432_2 (
    .pin1(load_1_mer), .pin2(goto_1_mer), .pin3(MER));  // open: pin4, pin5, pin6, pin13, pin12, pin11, pin10, pin9, pin8
  GATE_8 gate_8_6 (.EN(MOV_8), .DIn(mov8_1_load), .DOut(gate_8_6_dout));
  GATE_8 gate_8_7 (.EN(LOAD_8), .DIn(load_1_reg_load), .DOut(gate_8_7_dout));
  OR_8 or_8_1 (.IN_1(gate_8_6_dout), .IN_2(gate_8_7_dout), .OUT_1(REG_LOAD));
  GATE_8 gate_8_8 (.EN(MOV_8), .DIn(mov8_1_sel), .DOut(gate_8_8_dout));
  GATE_8 gate_8_9 (.EN(SAVE_8), .DIn(save_1_reg_select), .DOut(gate_8_9_dout));
  OR_8 or_8_2 (.IN_1(gate_8_8_dout), .IN_2(gate_8_9_dout), .OUT_1(or_8_2_out_1));
  OR_8 or_8_3 (.IN_1(REG_IN), .IN_2(or_8_2_out_1), .OUT_1(REG_SELECT));

  assign AT_08 = 1'b1;
endmodule

module LOAD (
  input  [7:0] INST,
  input  [23:0] SQC,
  output [7:0] REG_LOAD,
  output MSEL,
  output PCSEL,
  output MER
);

  wire n7404_1_pin2, n7432_1_pin3, n7432_1_pin8, n7432_1_pin11, n74245_1_pin1;
  wire [2:2] pull_resistor_1_node;
  wire [7:0] threetoeight_1_o_111;

  Pull_Resistor pull_resistor_1 (.node(pull_resistor_1_node[2]));
  _7432 #(.ShowInternalStructure("true")) u_7432_1 (
    .pin1(SQC[8]), .pin2(SQC[7]), .pin3(n7432_1_pin3), .pin4(n7432_1_pin3), .pin5(SQC[6]), .pin6(MSEL),
    .pin13(SQC[8]), .pin12(SQC[7]), .pin11(n7432_1_pin11), .pin10(n7432_1_pin11), .pin9(SQC[6]),
    .pin8(n7432_1_pin8));
  _7432 #(.ShowInternalStructure("true")) u_7432_2 (
    .pin13(SQC[10]), .pin12(SQC[9]), .pin11(PCSEL));  // open: pin1, pin2, pin3, pin4, pin5, pin6, pin10, pin9, pin8
  ThreeToEight threetoeight_1 (
    .FIn({pull_resistor_1_node[2], INST[1:0]}), .O_111(threetoeight_1_o_111[0]),
    .O_110(threetoeight_1_o_111[1]), .O_101(threetoeight_1_o_111[2]), .O_100(threetoeight_1_o_111[3]),
    .O_011(threetoeight_1_o_111[4]), .O_010(threetoeight_1_o_111[5]), .O_001(threetoeight_1_o_111[6]),
    .O_000(threetoeight_1_o_111[7]));
  _7404 #(.ShowInternalStructure("true")) u_7404_1 (
    .pin1(n7432_1_pin8), .pin2(n7404_1_pin2));  // open: pin3, pin4, pin5, pin6, pin13, pin12, pin11, pin10, pin9, pin8
  _74245 #(.ShowInternalStructure("true")) u_74245_1 (
    .pin1(n74245_1_pin1), .pin2(threetoeight_1_o_111[0]), .pin3(threetoeight_1_o_111[1]),
    .pin4(threetoeight_1_o_111[2]), .pin5(threetoeight_1_o_111[3]), .pin6(threetoeight_1_o_111[4]),
    .pin7(threetoeight_1_o_111[5]), .pin8(threetoeight_1_o_111[6]), .pin9(threetoeight_1_o_111[7]),
    .pin19(n7404_1_pin2), .pin18(REG_LOAD[0]), .pin17(REG_LOAD[1]), .pin16(REG_LOAD[2]), .pin15(REG_LOAD[3]),
    .pin14(REG_LOAD[4]), .pin13(REG_LOAD[5]), .pin12(REG_LOAD[6]), .pin11(REG_LOAD[7]));

  assign MER = SQC[7];
  // also tied to VCC on the sheet: n74245_1_pin1
endmodule

module SAVE (
  input  [7:0] INSTR,
  input  [23:0] SQC,
  output [7:0] REG_SELECT,
  output MSEL,
  output PCSEL,
  output MEW
);

  wire n7404_1_pin2, n7408_1_pin2, n7408_1_pin3, n7408_1_pin11, n7408_2_pin4, n7408_2_pin13, n7432_1_pin3,
       n7432_1_pin11, n74245_1_pin1;
  wire [7:0] n7408_2_pin11;

  _7408 #(.ShowInternalStructure("true")) u_7408_1 (
    .pin1(INSTR[1]), .pin2(n7408_1_pin2), .pin3(n7408_1_pin3), .pin13(n7408_1_pin2), .pin12(INSTR[0]),
    .pin11(n7408_1_pin11));  // open: pin4, pin5, pin6, pin10, pin9, pin8
  _7432 #(.ShowInternalStructure("true")) u_7432_1 (
    .pin1(SQC[7]), .pin2(SQC[8]), .pin3(n7432_1_pin3), .pin4(n7432_1_pin3), .pin5(SQC[6]), .pin6(MSEL),
    .pin13(SQC[8]), .pin12(SQC[7]), .pin11(n7432_1_pin11), .pin10(n7432_1_pin11), .pin9(SQC[6]),
    .pin8(n7408_1_pin2));
  _7432 #(.ShowInternalStructure("true")) u_7432_2 (
    .pin13(SQC[10]), .pin12(SQC[9]), .pin11(PCSEL));  // open: pin1, pin2, pin3, pin4, pin5, pin6, pin10, pin9, pin8
  _7408 #(.ShowInternalStructure("true")) u_7408_2 (
    .pin1(n7408_1_pin11), .pin2(n7408_1_pin3), .pin3(n7408_2_pin11[3]), .pin4(n7408_2_pin4),
    .pin5(n7408_1_pin11), .pin6(n7408_2_pin11[1]), .pin13(n7408_2_pin13), .pin12(n7408_2_pin4),
    .pin11(n7408_2_pin11[0]), .pin10(n7408_2_pin13), .pin9(n7408_1_pin3), .pin8(n7408_2_pin11[2]));
  Pull_Resistor pull_resistor_1 (.node(n7408_2_pin11[4]));
  Pull_Resistor pull_resistor_2 (.node(n7408_2_pin11[5]));
  Pull_Resistor pull_resistor_3 (.node(n7408_2_pin11[6]));
  Pull_Resistor pull_resistor_4 (.node(n7408_2_pin11[7]));
  _7404 #(.ShowInternalStructure("true")) u_7404_1 (
    .pin1(n7408_1_pin2), .pin2(n7404_1_pin2), .pin3(n7408_1_pin3), .pin4(n7408_2_pin4), .pin5(n7408_1_pin11),
    .pin6(n7408_2_pin13));  // open: pin13, pin12, pin11, pin10, pin9, pin8
  _74245 #(.ShowInternalStructure("true")) u_74245_1 (
    .pin1(n74245_1_pin1), .pin2(n7408_2_pin11[0]), .pin3(n7408_2_pin11[1]), .pin4(n7408_2_pin11[2]),
    .pin5(n7408_2_pin11[3]), .pin6(n7408_2_pin11[4]), .pin7(n7408_2_pin11[5]), .pin8(n7408_2_pin11[6]),
    .pin9(n7408_2_pin11[7]), .pin19(n7404_1_pin2), .pin18(REG_SELECT[0]), .pin17(REG_SELECT[1]),
    .pin16(REG_SELECT[2]), .pin15(REG_SELECT[3]), .pin14(REG_SELECT[4]), .pin13(REG_SELECT[5]),
    .pin12(REG_SELECT[6]), .pin11(REG_SELECT[7]));

  assign MEW = SQC[7];
  // also tied to VCC on the sheet: n74245_1_pin1
endmodule

module GATE_8 (
  input  EN,
  input  [7:0] DIn,
  output [7:0] DOut
);

  wire n7404_1_pin6, n74245_1_pin1;

  Pull_Resistor pull_resistor_1 (.node(DIn));
  _7404 #(.ShowInternalStructure("true")) u_7404_1 (
    .pin5(EN), .pin6(n7404_1_pin6));  // open: pin1, pin2, pin3, pin4, pin13, pin12, pin11, pin10, pin9, pin8
  _74245 #(.ShowInternalStructure("true")) u_74245_1 (
    .pin1(n74245_1_pin1), .pin2(DIn[0]), .pin3(DIn[1]), .pin4(DIn[2]), .pin5(DIn[3]), .pin6(DIn[4]),
    .pin7(DIn[5]), .pin8(DIn[6]), .pin9(DIn[7]), .pin19(n7404_1_pin6), .pin18(DOut[0]), .pin17(DOut[1]),
    .pin16(DOut[2]), .pin15(DOut[3]), .pin14(DOut[4]), .pin13(DOut[5]), .pin12(DOut[6]), .pin11(DOut[7]));
  Pull_Resistor pull_resistor_2 (.node(DOut));
  // also tied to VCC on the sheet: n74245_1_pin1
endmodule

module GATE_24 (
  input  EN,
  input  [23:0] DIn,
  output [23:0] DOut
);

  wire n7404_1_pin6, n74245_1_pin1, n74245_2_pin1, n74245_3_pin1;

  _7404 #(.ShowInternalStructure("true")) u_7404_1 (
    .pin5(EN), .pin6(n7404_1_pin6));  // open: pin1, pin2, pin3, pin4, pin13, pin12, pin11, pin10, pin9, pin8
  _74245 #(.ShowInternalStructure("true")) u_74245_1 (
    .pin1(n74245_1_pin1), .pin2(DIn[0]), .pin3(DIn[1]), .pin4(DIn[2]), .pin5(DIn[3]), .pin6(DIn[4]),
    .pin7(DIn[5]), .pin8(DIn[6]), .pin9(DIn[7]), .pin19(n7404_1_pin6), .pin18(DOut[0]), .pin17(DOut[1]),
    .pin16(DOut[2]), .pin15(DOut[3]), .pin14(DOut[4]), .pin13(DOut[5]), .pin12(DOut[6]), .pin11(DOut[7]));
  _74245 #(.ShowInternalStructure("true")) u_74245_2 (
    .pin1(n74245_2_pin1), .pin2(DIn[8]), .pin3(DIn[9]), .pin4(DIn[10]), .pin5(DIn[11]), .pin6(DIn[12]),
    .pin7(DIn[13]), .pin8(DIn[14]), .pin9(DIn[15]), .pin19(n7404_1_pin6), .pin18(DOut[8]), .pin17(DOut[9]),
    .pin16(DOut[10]), .pin15(DOut[11]), .pin14(DOut[12]), .pin13(DOut[13]), .pin12(DOut[14]), .pin11(DOut[15]));
  _74245 #(.ShowInternalStructure("true")) u_74245_3 (
    .pin1(n74245_3_pin1), .pin2(DIn[16]), .pin3(DIn[17]), .pin4(DIn[18]), .pin5(DIn[19]), .pin6(DIn[20]),
    .pin7(DIn[21]), .pin8(DIn[22]), .pin9(DIn[23]), .pin19(n7404_1_pin6), .pin18(DOut[16]), .pin17(DOut[17]),
    .pin16(DOut[18]), .pin15(DOut[19]), .pin14(DOut[20]), .pin13(DOut[21]), .pin12(DOut[22]), .pin11(DOut[23]));
  // also tied to VCC on the sheet: {n74245_1_pin1, n74245_2_pin1, n74245_3_pin1}
endmodule

module setab (
  input  [7:0] INSTR,
  input  [23:0] SQC,
  output A_LOAD,
  output B_LOAD,
  output [7:0] DOut
);

  wire n7404_1_pin8, n7432_1_pin8, n7432_1_pin11;

  _7404 #(.ShowInternalStructure("true")) u_7404_1 (
    .pin9(INSTR[5]), .pin8(n7404_1_pin8));  // open: pin1, pin2, pin3, pin4, pin5, pin6, pin13, pin12, pin11, pin10
  _7432 #(.ShowInternalStructure("true")) u_7432_1 (
    .pin13(SQC[9]), .pin12(SQC[8]), .pin11(n7432_1_pin11), .pin10(n7432_1_pin11), .pin9(SQC[7]),
    .pin8(n7432_1_pin8));  // open: pin1, pin2, pin3, pin4, pin5, pin6
  _7408 #(.ShowInternalStructure("true")) u_7408_1 (
    .pin13(n7404_1_pin8), .pin12(SQC[8]), .pin11(A_LOAD), .pin10(INSTR[5]), .pin9(SQC[8]), .pin8(B_LOAD));  // open: pin1, pin2, pin3, pin4, pin5, pin6
  GATE_8 gate_8_1 (.EN(n7432_1_pin8), .DIn({INSTR[0], INSTR[1], INSTR[2], INSTR[3], {4{INSTR[4]}}}), .DOut(DOut));
endmodule

module GOTO (
  input  [7:0] INSTR,
  input  [2:0] COND_REG,
  input  [23:0] SQC,
  output J1LOAD,
  output M1LOAD,
  output J2LOAD,
  output M2LOAD,
  output MER,
  output INCLOAD,
  output JSEL,
  output MSEL,
  output PCSEL,
  output PCLOAD,
  output INCSEL
);

  wire n7404_1_pin2, n7404_1_pin3, n7404_1_pin4, n7404_1_pin5, n7404_1_pin6, n7404_1_pin8, n7404_1_pin9,
       n7404_1_pin10, n7404_1_pin11, n7404_1_pin12, n7408_2_pin3, n7408_2_pin6, n7408_2_pin11, n7408_5_pin3,
       n7408_5_pin6, n7408_5_pin8, n7408_5_pin11, n7432_1_pin3, n7432_1_pin6, n7432_1_pin8, n7432_1_pin11,
       n7432_2_pin3, n7432_2_pin6, n7432_2_pin8, n7432_2_pin11, n7432_3_pin3, n7432_3_pin6, n7432_3_pin8,
       n7432_3_pin11, n7432_4_pin3, n7432_4_pin4, n7432_4_pin6, n7432_4_pin11, n7432_5_pin9, n7432_5_pin11,
       n7432_7_pin6, n7432_7_pin8, n7432_7_pin11, n7432_8_pin5, n7432_8_pin6, n7432_9_pin3, n7432_9_pin6;
  wire [7:0] dual_regist_b_c_1_bout;

  _7432 #(.ShowInternalStructure("true")) u_7432_1 (
    .pin1(SQC[5]), .pin2(SQC[6]), .pin3(n7432_1_pin3), .pin4(n7432_1_pin3), .pin5(SQC[7]),
    .pin6(n7432_1_pin6), .pin13(SQC[5]), .pin12(SQC[6]), .pin11(n7432_1_pin11), .pin10(n7432_1_pin11),
    .pin9(SQC[7]), .pin8(n7432_1_pin8));
  _7432 #(.ShowInternalStructure("true")) u_7432_2 (
    .pin1(SQC[11]), .pin2(SQC[12]), .pin3(n7432_2_pin3), .pin4(SQC[13]), .pin5(SQC[14]), .pin6(n7432_2_pin6),
    .pin13(SQC[8]), .pin12(SQC[9]), .pin11(n7432_2_pin11), .pin10(n7432_2_pin11), .pin9(SQC[10]),
    .pin8(n7432_2_pin8));
  _7404 #(.ShowInternalStructure("true")) u_7404_1 (
    .pin1(dual_regist_b_c_1_bout[5]), .pin2(n7404_1_pin2), .pin3(n7404_1_pin3), .pin4(n7404_1_pin4),
    .pin5(n7404_1_pin5), .pin6(n7404_1_pin6), .pin13(COND_REG[2]), .pin12(n7404_1_pin12),
    .pin11(n7404_1_pin11), .pin10(n7404_1_pin10), .pin9(n7404_1_pin9), .pin8(n7404_1_pin8));
  _7432 #(.ShowInternalStructure("true")) u_7432_3 (
    .pin1(n7432_2_pin6), .pin2(SQC[15]), .pin3(n7432_3_pin3), .pin4(SQC[16]), .pin5(SQC[17]),
    .pin6(n7432_3_pin6), .pin13(SQC[13]), .pin12(SQC[14]), .pin11(n7432_3_pin11), .pin10(n7432_3_pin11),
    .pin9(SQC[15]), .pin8(n7432_3_pin8));
  _7432 #(.ShowInternalStructure("true")) u_7432_4 (
    .pin1(n7432_3_pin6), .pin2(SQC[18]), .pin3(n7432_4_pin3), .pin4(n7432_4_pin4), .pin5(SQC[23]),
    .pin6(n7432_4_pin6), .pin13(SQC[19]), .pin12(SQC[20]), .pin11(n7432_4_pin11), .pin10(SQC[21]),
    .pin9(SQC[22]), .pin8(n7432_4_pin4));
  Dual_Regist_B_C dual_regist_b_c_1 (
    .DIn(INSTR), .CLK(SQC[5]), .LOAD1(SQC[5]), .BOut(dual_regist_b_c_1_bout));  // open: LOAD2, SELECT1, SELECT2, LOAD12, SELECT12, D16In, COut, D16Out
  _7432 #(.ShowInternalStructure("true")) u_7432_5 (
    .pin13(SQC[20]), .pin12(SQC[19]), .pin11(n7432_5_pin11), .pin10(n7432_5_pin11), .pin9(n7432_5_pin9));  // open: pin1, pin2, pin3, pin4, pin5, pin6, pin8
  _7404 #(.ShowInternalStructure("true")) u_7404_2 (
    .pin13(SQC[21]), .pin12(n7432_5_pin9));  // open: pin1, pin2, pin3, pin4, pin5, pin6, pin11, pin10, pin9, pin8
  _7408 #(.ShowInternalStructure("true")) u_7408_1 (
    .pin1(COND_REG[1]), .pin2(dual_regist_b_c_1_bout[4]), .pin3(n7404_1_pin11), .pin4(COND_REG[0]),
    .pin5(dual_regist_b_c_1_bout[3]), .pin6(n7404_1_pin9), .pin13(dual_regist_b_c_1_bout[2]),
    .pin12(COND_REG[2]), .pin11(n7404_1_pin3), .pin10(dual_regist_b_c_1_bout[1]), .pin9(n7404_1_pin12),
    .pin8(n7404_1_pin5));
  _7408 #(.ShowInternalStructure("true")) u_7408_2 (
    .pin1(n7404_1_pin10), .pin2(n7404_1_pin8), .pin3(n7408_2_pin3), .pin4(n7408_2_pin3), .pin5(n7404_1_pin4),
    .pin6(n7408_2_pin6), .pin13(n7408_2_pin6), .pin12(n7404_1_pin6), .pin11(n7408_2_pin11));  // open: pin10, pin9, pin8
  _7432 #(.ShowInternalStructure("true")) u_7432_6 (
    .pin9(SQC[9]), .pin8(INCLOAD));  // open: pin1, pin2, pin3, pin4, pin5, pin6, pin13, pin12, pin11, pin10
  _7408 #(.ShowInternalStructure("true")) u_7408_3 (
    .pin1(SQC[6]), .pin2(dual_regist_b_c_1_bout[5]), .pin3(J1LOAD), .pin4(SQC[6]), .pin5(n7404_1_pin2),
    .pin6(M1LOAD), .pin13(dual_regist_b_c_1_bout[5]), .pin12(SQC[14]), .pin11(J2LOAD), .pin10(n7404_1_pin2),
    .pin9(SQC[14]), .pin8(M2LOAD));
  _7432 #(.ShowInternalStructure("true")) u_7432_7 (
    .pin1(n7432_1_pin6), .pin2(n7432_3_pin8), .pin3(MER), .pin4(SQC[11]), .pin5(SQC[17]),
    .pin6(n7432_7_pin6), .pin13(n7432_1_pin8), .pin12(n7432_2_pin8), .pin11(n7432_7_pin11),
    .pin10(n7432_4_pin3), .pin9(n7432_2_pin3), .pin8(n7432_7_pin8));
  _7432 #(.ShowInternalStructure("true")) u_7432_8 (
    .pin4(n7432_7_pin6), .pin5(n7432_8_pin5), .pin6(n7432_8_pin6), .pin13(n7432_7_pin11),
    .pin12(n7432_3_pin3), .pin11(PCSEL), .pin10(n7432_7_pin8), .pin9(n7432_4_pin6), .pin8(INCSEL));  // open: pin1, pin2, pin3
  _7408 #(.ShowInternalStructure("true")) u_7408_4 (
    .pin1(n7404_1_pin2), .pin2(n7432_4_pin11), .pin3(MSEL), .pin4(dual_regist_b_c_1_bout[5]),
    .pin5(n7432_4_pin11), .pin6(JSEL), .pin9(n7408_2_pin11));  // open: pin13, pin12, pin11, pin10, pin8
  _7408 #(.ShowInternalStructure("true")) u_7408_5 (
    .pin1(SQC[19]), .pin2(n7404_1_pin3), .pin3(n7408_5_pin3), .pin4(SQC[19]), .pin5(n7404_1_pin5),
    .pin6(n7408_5_pin6), .pin13(n7404_1_pin9), .pin12(SQC[19]), .pin11(n7408_5_pin11), .pin10(SQC[19]),
    .pin9(n7404_1_pin11), .pin8(n7408_5_pin8));
  _7432 #(.ShowInternalStructure("true")) u_7432_9 (
    .pin1(n7408_5_pin6), .pin2(n7408_5_pin3), .pin3(n7432_9_pin3), .pin4(n7432_9_pin3), .pin5(n7408_5_pin11),
    .pin6(n7432_9_pin6), .pin13(n7432_9_pin6), .pin12(n7408_5_pin8), .pin11(n7432_8_pin5),
    .pin10(n7432_8_pin6), .pin9(n7432_4_pin4), .pin8(PCLOAD));
endmodule

module OR_8 (
  input  [7:0] IN_1,
  input  [7:0] IN_2,
  output [7:0] OUT_1
);

  Pull_Resistor pull_resistor_1 (.node(IN_1));
  _7432 #(.ShowInternalStructure("true")) u_7432_1 (
    .pin1(IN_1[0]), .pin2(IN_2[0]), .pin3(OUT_1[0]), .pin4(IN_1[1]), .pin5(IN_2[1]), .pin6(OUT_1[1]),
    .pin13(IN_1[2]), .pin12(IN_2[2]), .pin11(OUT_1[2]), .pin10(IN_1[3]), .pin9(IN_2[3]), .pin8(OUT_1[3]));
  _7432 #(.ShowInternalStructure("true")) u_7432_2 (
    .pin1(IN_1[4]), .pin2(IN_2[4]), .pin3(OUT_1[4]), .pin4(IN_1[5]), .pin5(IN_2[5]), .pin6(OUT_1[5]),
    .pin13(IN_1[6]), .pin12(IN_2[6]), .pin11(OUT_1[6]), .pin10(IN_1[7]), .pin9(IN_2[7]), .pin8(OUT_1[7]));
endmodule

module Testbett (
  input  in_1,
  input  in_2
);

  wire n7404_1_pin12;

  _7404 #(.ShowInternalStructure("true")) u_7404_1 (.pin12(n7404_1_pin12));  // open: pin1, pin2, pin3, pin4, pin5, pin6, pin13, pin11, pin10, pin9, pin8
  _7408 #(.ShowInternalStructure("true")) u_7408_1 (.pin1(n7404_1_pin12));  // open: pin2, pin3, pin4, pin5, pin6, pin13, pin12, pin11, pin10, pin9, pin8
  _7474 #(.ShowInternalStructure("true")) u_7474_1 (
    .pin2(in_1), .pin3(in_2));  // open: pin1, pin4, pin5, pin6, pin13, pin12, pin11, pin10, pin9, pin8
endmodule

module Conv_16_to_14 (
  input  [15:0] IN_0,
  output [13:0] OUT_0
);


  assign OUT_0 = IN_0[13:0];
endmodule

module OUT_8 (
  input  [7:0] INSTR,
  input  [23:0] SQC,
  output [7:0] REG_SELECT,
  output OUT8
);

  wire n7432_1_pin3, n7432_1_pin6;
  wire [2:1] pull_resistor_3_node;
  wire [7:0] threetoeight_1_o_000;

  Pull_Resistor pull_resistor_1 (.node(pull_resistor_3_node[2]));
  Pull_Resistor pull_resistor_2 (.node(SQC));
  Pull_Resistor pull_resistor_3 (.node(pull_resistor_3_node[1]));
  _7432 #(.ShowInternalStructure("true")) u_7432_1 (
    .pin1(SQC[8]), .pin2(SQC[7]), .pin3(n7432_1_pin3), .pin4(n7432_1_pin3), .pin5(SQC[6]), .pin6(n7432_1_pin6));  // open: pin13, pin12, pin11, pin10, pin9, pin8
  ThreeToEight threetoeight_1 (
    .FIn({pull_resistor_3_node, INSTR[0]}), .O_001(threetoeight_1_o_000[3]), .O_000(threetoeight_1_o_000[0]));  // open: O_111, O_110, O_101, O_100, O_011, O_010
  Pull_Resistor pull_resistor_4 (.node(threetoeight_1_o_000[1]));
  Pull_Resistor pull_resistor_5 (.node(threetoeight_1_o_000[2]));
  Pull_Resistor pull_resistor_6 (.node(threetoeight_1_o_000[4]));
  Pull_Resistor pull_resistor_7 (.node(threetoeight_1_o_000[5]));
  Pull_Resistor pull_resistor_8 (.node(threetoeight_1_o_000[6]));
  Pull_Resistor pull_resistor_9 (.node(threetoeight_1_o_000[7]));
  GATE_8 gate_8_1 (.EN(n7432_1_pin6), .DIn(threetoeight_1_o_000), .DOut(REG_SELECT));

  assign OUT8 = SQC[7];
endmodule

module Output_Register (
  input  [7:0] DIn,
  input  CLK,
  input  OUT8,
  input  [7:0] INSTR,
  input  [23:0] SQC,
  output [7:0] DISP_OUT,
  output [7:0] REG_SELECT
);

  wire n7432_1_pin1, n7432_1_pin2, n7432_1_pin3, n7432_1_pin5, n74245_1_pin1, n74245_1_pin19, n74273_1_pin11,
       out_8_1_out8;
  wire [7:0] gate_8_1_dout, n74245_1_pin18;
  wire [23:0] gate_24_1_dout;

  GATE_8 gate_8_1 (.EN(OUT8), .DIn(INSTR), .DOut(gate_8_1_dout));
  GATE_24 gate_24_1 (.EN(OUT8), .DIn(SQC), .DOut(gate_24_1_dout));
  OUT_8 out_8_1 (.INSTR(gate_8_1_dout), .SQC(gate_24_1_dout), .REG_SELECT(REG_SELECT), .OUT8(out_8_1_out8));
  _74245 #(.ShowInternalStructure("true")) u_74245_1 (
    .pin1(n74245_1_pin1), .pin2(DIn[0]), .pin3(DIn[1]), .pin4(DIn[2]), .pin5(DIn[3]), .pin6(DIn[4]),
    .pin7(DIn[5]), .pin8(DIn[6]), .pin9(DIn[7]), .pin19(n74245_1_pin19), .pin18(n74245_1_pin18[0]),
    .pin17(n74245_1_pin18[1]), .pin16(n74245_1_pin18[2]), .pin15(n74245_1_pin18[3]),
    .pin14(n74245_1_pin18[4]), .pin13(n74245_1_pin18[5]), .pin12(n74245_1_pin18[6]), .pin11(n74245_1_pin18[7]));
  Pull_Resistor pull_resistor_1 (.node(n74245_1_pin18));
  _7404 #(.ShowInternalStructure("true")) u_7404_1 (
    .pin11(out_8_1_out8), .pin10(n74245_1_pin19));  // open: pin1, pin2, pin3, pin4, pin5, pin6, pin13, pin12, pin9, pin8
  _74273 #(.ShowInternalStructure("true")) u_74273_1 (
    .pin2(DISP_OUT[0]), .pin3(n74245_1_pin18[0]), .pin4(n74245_1_pin18[1]), .pin5(DISP_OUT[1]),
    .pin6(DISP_OUT[2]), .pin7(n74245_1_pin18[2]), .pin8(n74245_1_pin18[3]), .pin9(DISP_OUT[3]),
    .pin19(DISP_OUT[7]), .pin18(n74245_1_pin18[7]), .pin17(n74245_1_pin18[6]), .pin16(DISP_OUT[6]),
    .pin15(DISP_OUT[5]), .pin14(n74245_1_pin18[5]), .pin13(n74245_1_pin18[4]), .pin12(DISP_OUT[4]),
    .pin11(n74273_1_pin11));  // open: pin1
  _7432 #(.ShowInternalStructure("true")) u_7432_1 (
    .pin1(n7432_1_pin1), .pin2(n7432_1_pin2), .pin3(n7432_1_pin3), .pin4(n7432_1_pin2), .pin5(n7432_1_pin5),
    .pin6(n74273_1_pin11));  // open: pin13, pin12, pin11, pin10, pin9, pin8
  _7408 #(.ShowInternalStructure("true")) u_7408_1 (
    .pin1(out_8_1_out8), .pin2(CLK), .pin3(n7432_1_pin5), .pin4(CLK), .pin6(n7432_1_pin1), .pin12(CLK),
    .pin11(n7432_1_pin2));  // open: pin5, pin13, pin10, pin9, pin8
  // also tied to VCC on the sheet: n74245_1_pin1
endmodule

module Serial_IO (
  input  in_1,
  input  in_2,
  input  in_3,
  input  in_4,
  output SRL_OUT,
  output N_SRL_OUT
);

  wire n7411_1_pin1, n7411_1_pin8, n7411_1_pin9, n7411_1_pin10, n7411_1_pin12, n74165_1_pin1, n74165_1_pin3,
       n74165_1_pin4, n74165_1_pin5, n74165_1_pin6, n74165_1_pin11, n74165_1_pin12, n74165_1_pin13,
       n74165_1_pin14, n74192_1_pin1, n74192_1_pin2, n74192_1_pin3, n74192_1_pin5, n74192_1_pin6,
       n74192_1_pin7;

  _74192 #(.ShowInternalStructure("true")) u_74192_1 (
    .pin1(n74192_1_pin1), .pin2(n74192_1_pin2), .pin3(n74192_1_pin3), .pin4(in_1), .pin5(n74192_1_pin5),
    .pin6(n74192_1_pin6), .pin7(n74192_1_pin7), .pin15(in_1), .pin14(in_3), .pin11(in_4),
    .pin10(n74192_1_pin1), .pin9(n74192_1_pin1));  // open: pin13, pin12
  _7411 #(.ShowInternalStructure("true")) u_7411_1 (
    .pin1(n7411_1_pin1), .pin2(n74192_1_pin3), .pin13(n74192_1_pin7), .pin12(n7411_1_pin12),
    .pin11(n7411_1_pin12), .pin10(n7411_1_pin10), .pin9(n7411_1_pin9), .pin8(n7411_1_pin8));  // open: pin3, pin4, pin5, pin6
  _74165 #(.ShowInternalStructure("true")) u_74165_1 (
    .pin1(n74165_1_pin1), .pin2(n74192_1_pin5), .pin3(n74165_1_pin3), .pin4(n74165_1_pin4),
    .pin5(n74165_1_pin5), .pin6(n74165_1_pin6), .pin7(N_SRL_OUT), .pin15(in_2), .pin14(n74165_1_pin14),
    .pin13(n74165_1_pin13), .pin12(n74165_1_pin12), .pin11(n74165_1_pin11), .pin9(SRL_OUT));  // open: pin10
  Clock clock_1 (.out(n74192_1_pin5));
  _7404 #(.ShowInternalStructure("true")) u_7404_1 (
    .pin1(n74192_1_pin2), .pin2(n7411_1_pin10), .pin3(n74192_1_pin6), .pin4(n7411_1_pin1),
    .pin13(n7411_1_pin8), .pin12(n74165_1_pin1));  // open: pin5, pin6, pin11, pin10, pin9, pin8
  _74273 #(.ShowInternalStructure("true")) u_74273_1 (
    .pin1(n7411_1_pin8), .pin2(n74165_1_pin11), .pin5(n74165_1_pin12), .pin6(n74165_1_pin13),
    .pin9(n74165_1_pin14), .pin19(n74165_1_pin6), .pin16(n74165_1_pin5), .pin15(n74165_1_pin4),
    .pin12(n74165_1_pin3));  // open: pin3, pin4, pin7, pin8, pin18, pin17, pin14, pin13, pin11
  // also tied to GND on the sheet: n74192_1_pin1
  // also tied to VCC on the sheet: n7411_1_pin9
endmodule

module Dual_Register_A_D (
  input  [7:0] DIn,
  input  CLK,
  input  LOAD1,
  input  LOAD2,
  input  SELECT1,
  input  SELECT2,
  input  LOAD12,
  input  SELECT12,
  input  [15:0] D16In,
  output [7:0] DOut,
  output [15:0] D16Out
);

  wire n7404_1_pin2, n7404_1_pin4, n7404_1_pin6, n7404_1_pin8, n7404_1_pin12, n7432_1_pin1, n7432_1_pin2,
       n7432_1_pin3, n7432_1_pin5, n74245_1_pin1, n74245_1_pin19, n74245_2_pin1, n74245_3_pin1,
       n74245_4_pin1, n74245_5_pin1, n74245_6_pin1, n74245_7_pin1, n74245_8_pin1, n74273_1_pin11;
  wire [7:0] n74245_1_pin11, n74245_3_pin18, n74273_1_pin19, n74273_2_pin2;

  _74245 #(.ShowInternalStructure("true")) u_74245_1 (
    .pin1(n74245_1_pin1), .pin2(DIn[0]), .pin3(DIn[1]), .pin4(DIn[2]), .pin5(DIn[3]), .pin6(DIn[4]),
    .pin7(DIn[5]), .pin8(DIn[6]), .pin9(DIn[7]), .pin19(n74245_1_pin19), .pin18(n74245_1_pin11[7]),
    .pin17(n74245_1_pin11[6]), .pin16(n74245_1_pin11[5]), .pin15(n74245_1_pin11[4]),
    .pin14(n74245_1_pin11[3]), .pin13(n74245_1_pin11[2]), .pin12(n74245_1_pin11[1]), .pin11(n74245_1_pin11[0]));
  Pull_Resistor pull_resistor_1 (.node(n74245_1_pin11));
  _7404 #(.ShowInternalStructure("true")) u_7404_1 (
    .pin1(SELECT2), .pin2(n7404_1_pin2), .pin3(SELECT12), .pin4(n7404_1_pin4), .pin5(LOAD12),
    .pin6(n7404_1_pin6), .pin13(SELECT1), .pin12(n7404_1_pin12), .pin11(LOAD1), .pin10(n74245_1_pin19),
    .pin9(LOAD2), .pin8(n7404_1_pin8));
  _74245 #(.ShowInternalStructure("true")) u_74245_2 (
    .pin1(n74245_2_pin1), .pin2(D16In[0]), .pin3(D16In[1]), .pin4(D16In[2]), .pin5(D16In[3]),
    .pin6(D16In[4]), .pin7(D16In[5]), .pin8(D16In[6]), .pin9(D16In[7]), .pin19(n7404_1_pin6),
    .pin18(n74245_1_pin11[0]), .pin17(n74245_1_pin11[1]), .pin16(n74245_1_pin11[2]),
    .pin15(n74245_1_pin11[3]), .pin14(n74245_1_pin11[4]), .pin13(n74245_1_pin11[5]),
    .pin12(n74245_1_pin11[6]), .pin11(n74245_1_pin11[7]));
  _74245 #(.ShowInternalStructure("true")) u_74245_3 (
    .pin1(n74245_3_pin1), .pin2(D16In[8]), .pin3(D16In[9]), .pin4(D16In[10]), .pin5(D16In[11]),
    .pin6(D16In[12]), .pin7(D16In[13]), .pin8(D16In[14]), .pin9(D16In[15]), .pin19(n7404_1_pin6),
    .pin18(n74245_3_pin18[0]), .pin17(n74245_3_pin18[1]), .pin16(n74245_3_pin18[2]),
    .pin15(n74245_3_pin18[3]), .pin14(n74245_3_pin18[4]), .pin13(n74245_3_pin18[5]),
    .pin12(n74245_3_pin18[6]), .pin11(n74245_3_pin18[7]));
  _74273 #(.ShowInternalStructure("true")) u_74273_1 (
    .pin2(n74273_1_pin19[7]), .pin3(n74245_1_pin11[0]), .pin4(n74245_1_pin11[1]), .pin5(n74273_1_pin19[6]),
    .pin6(n74273_1_pin19[5]), .pin7(n74245_1_pin11[2]), .pin8(n74245_1_pin11[3]), .pin9(n74273_1_pin19[4]),
    .pin19(n74273_1_pin19[0]), .pin18(n74245_1_pin11[7]), .pin17(n74245_1_pin11[6]),
    .pin16(n74273_1_pin19[1]), .pin15(n74273_1_pin19[2]), .pin14(n74245_1_pin11[5]),
    .pin13(n74245_1_pin11[4]), .pin12(n74273_1_pin19[3]), .pin11(n74273_1_pin11));  // open: pin1
  _7432 #(.ShowInternalStructure("true")) u_7432_1 (
    .pin1(n7432_1_pin1), .pin2(n7432_1_pin2), .pin3(n7432_1_pin3), .pin4(n7432_1_pin2), .pin5(n7432_1_pin5),
    .pin6(n74273_1_pin11));  // open: pin13, pin12, pin11, pin10, pin9, pin8
  _7408 #(.ShowInternalStructure("true")) u_7408_1 (
    .pin1(LOAD1), .pin2(CLK), .pin3(n7432_1_pin5), .pin4(CLK), .pin5(LOAD2), .pin6(n7432_1_pin1),
    .pin13(LOAD12), .pin12(CLK), .pin11(n7432_1_pin2));  // open: pin10, pin9, pin8
  _74245 #(.ShowInternalStructure("true")) u_74245_4 (
    .pin1(n74245_4_pin1), .pin2(DIn[7]), .pin3(DIn[6]), .pin4(DIn[5]), .pin5(DIn[4]), .pin6(DIn[3]),
    .pin7(DIn[2]), .pin8(DIn[1]), .pin9(DIn[0]), .pin19(n7404_1_pin8), .pin18(n74245_3_pin18[0]),
    .pin17(n74245_3_pin18[1]), .pin16(n74245_3_pin18[2]), .pin15(n74245_3_pin18[3]),
    .pin14(n74245_3_pin18[4]), .pin13(n74245_3_pin18[5]), .pin12(n74245_3_pin18[6]), .pin11(n74245_3_pin18[7]));
  Pull_Resistor pull_resistor_2 (.node(n74245_3_pin18));
  _74273 #(.ShowInternalStructure("true")) u_74273_2 (
    .pin2(n74273_2_pin2[0]), .pin3(n74245_3_pin18[0]), .pin4(n74245_3_pin18[1]), .pin5(n74273_2_pin2[1]),
    .pin6(n74273_2_pin2[2]), .pin7(n74245_3_pin18[2]), .pin8(n74245_3_pin18[3]), .pin9(n74273_2_pin2[3]),
    .pin19(n74273_2_pin2[7]), .pin18(n74245_3_pin18[7]), .pin17(n74245_3_pin18[6]), .pin16(n74273_2_pin2[6]),
    .pin15(n74273_2_pin2[5]), .pin14(n74245_3_pin18[5]), .pin13(n74245_3_pin18[4]), .pin12(n74273_2_pin2[4]),
    .pin11(n7432_1_pin3));  // open: pin1
  _74245 #(.ShowInternalStructure("true")) u_74245_5 (
    .pin1(n74245_5_pin1), .pin2(n74273_1_pin19[7]), .pin3(n74273_1_pin19[6]), .pin4(n74273_1_pin19[5]),
    .pin5(n74273_1_pin19[4]), .pin6(n74273_1_pin19[3]), .pin7(n74273_1_pin19[2]), .pin8(n74273_1_pin19[1]),
    .pin9(n74273_1_pin19[0]), .pin19(n7404_1_pin12), .pin18(DOut[7]), .pin17(DOut[6]), .pin16(DOut[5]),
    .pin15(DOut[4]), .pin14(DOut[3]), .pin13(DOut[2]), .pin12(DOut[1]), .pin11(DOut[0]));
  _74245 #(.ShowInternalStructure("true")) u_74245_6 (
    .pin1(n74245_6_pin1), .pin2(n74273_2_pin2[7]), .pin3(n74273_2_pin2[6]), .pin4(n74273_2_pin2[5]),
    .pin5(n74273_2_pin2[4]), .pin6(n74273_2_pin2[3]), .pin7(n74273_2_pin2[2]), .pin8(n74273_2_pin2[1]),
    .pin9(n74273_2_pin2[0]), .pin19(n7404_1_pin2), .pin18(DOut[7]), .pin17(DOut[6]), .pin16(DOut[5]),
    .pin15(DOut[4]), .pin14(DOut[3]), .pin13(DOut[2]), .pin12(DOut[1]), .pin11(DOut[0]));
  _74245 #(.ShowInternalStructure("true")) u_74245_7 (
    .pin1(n74245_7_pin1), .pin2(n74273_1_pin19[0]), .pin3(n74273_1_pin19[1]), .pin4(n74273_1_pin19[2]),
    .pin5(n74273_1_pin19[3]), .pin6(n74273_1_pin19[4]), .pin7(n74273_1_pin19[5]), .pin8(n74273_1_pin19[6]),
    .pin9(n74273_1_pin19[7]), .pin19(n7404_1_pin4), .pin18(D16Out[7]), .pin17(D16Out[6]), .pin16(D16Out[5]),
    .pin15(D16Out[4]), .pin14(D16Out[3]), .pin13(D16Out[2]), .pin12(D16Out[1]), .pin11(D16Out[0]));
  _74245 #(.ShowInternalStructure("true")) u_74245_8 (
    .pin1(n74245_8_pin1), .pin2(n74273_2_pin2[0]), .pin3(n74273_2_pin2[1]), .pin4(n74273_2_pin2[2]),
    .pin5(n74273_2_pin2[3]), .pin6(n74273_2_pin2[4]), .pin7(n74273_2_pin2[5]), .pin8(n74273_2_pin2[6]),
    .pin9(n74273_2_pin2[7]), .pin19(n7404_1_pin4), .pin18(D16Out[8]), .pin17(D16Out[9]), .pin16(D16Out[10]),
    .pin15(D16Out[11]), .pin14(D16Out[12]), .pin13(D16Out[13]), .pin12(D16Out[14]), .pin11(D16Out[15]));
  // also tied to VCC on the sheet: {n74245_1_pin1, n74245_2_pin1, n74245_3_pin1, n74245_4_pin1, n74245_5_pin1, n74245_6_pin1, n74245_7_pin1, n74245_8_pin1}
endmodule
